// Logisim project Processor.circ as structural Verilog: 30 circuits, main circuit main
module main (
  input  [9:0] Address_to_Jump,
  input  in_2,
  input  in_3,
  input  in_4,
  output [9:0] PC_Output,
  output [17:0] INSTRUCTION
);

  wire clock_1_out, control_unit_1_p6, control_unit_1_p7, control_unit_1_p8;
  wire [3:0] control_unit_1_p2, control_unit_1_p3, control_unit_1_p4;
  wire [9:0] control_unit_1_p5;
  wire [17:0] alu_1_out, multiplexer_1_out, register_file_1_r1_data, register_file_1_r2_data,
       sign_extender_1__18_bit_input;

  Clock clock_1 (.out(clock_1_out));
  Program_Counter program_counter_1 (
    .Input(Address_to_Jump), .Increment(in_2), .Write_Address(in_3), .Output(PC_Output), .Reset(in_4),
    .Clock(clock_1_out));
  // Control_Unit control_unit_1: pin names not known; wires that end beside it: INSTRUCTION, control_unit_1_p2, control_unit_1_p3, control_unit_1_p4, control_unit_1_p5, control_unit_1_p6, control_unit_1_p7, control_unit_1_p8
  Sign_Extender sign_extender_1 (._10_bit_Input(control_unit_1_p5), ._18_bit_Input(sign_extender_1__18_bit_input));
  RAM #(.addrWidth(10), .dataWidth(18)) ram_1 (
    .addr(PC_Output), .data(INSTRUCTION), .sel(1'b1), .ld(1'b1));  // open: clk, clr
  Register_File register_file_1 (
    .W_Data(alu_1_out), .W_Address(control_unit_1_p2), .Reset(in_4), .R1_Data(register_file_1_r1_data),
    .Clock(clock_1_out), .W_Enabled(control_unit_1_p7), .R2_Data(register_file_1_r2_data),
    .R2_Address(control_unit_1_p4), .R1_Address(control_unit_1_p3));
  Multiplexer #(.width(18), .enable("false")) multiplexer_1 (
    .in0(register_file_1_r2_data), .in1(sign_extender_1__18_bit_input), .out(multiplexer_1_out),
    .sel(control_unit_1_p8));
  ALU alu_1 (
    .ADD(control_unit_1_p6), .AND(1'b0), .NAND(1'b0), .NOR(1'b0), .A(register_file_1_r1_data),
    .B(multiplexer_1_out), .Out(alu_1_out));

  // Notes on the sheet:
  //   RAM
  //   Careful: To get the first 4 bits of instuction, you have to get bits: 17,16,15,14
endmodule

module JE (
  input  ZF,
  input  CF,
  output writeADDR
);

  wire not_1_out;

  not not_1 (not_1_out, CF);
  and and_1 (writeADDR, ZF, not_1_out);
endmodule

module JA (
  input  ZF,
  input  CF,
  output writeADDR
);

  wire not_1_out, not_2_out;

  not not_1 (not_1_out, ZF);
  not not_2 (not_2_out, CF);
  and and_1 (writeADDR, not_1_out, not_2_out);
endmodule

module JB (
  input  ZF,
  input  CF,
  output writeADDR
);

  wire not_1_out;

  not not_1 (not_1_out, ZF);
  and and_1 (writeADDR, not_1_out, CF);
endmodule

module JAE (
  input  CF,
  output writeADDR
);

  not not_1 (writeADDR, CF);
endmodule

module JBE (
  input  ZF,
  input  CF,
  output writeADDR
);

  and and_1 (writeADDR, ZF, CF);
endmodule

module Program_Counter (
  input  [9:0] Input,
  input  Increment,
  input  Clock,
  input  Write_Address,
  input  Reset,
  output [9:0] Output
);

  wire [9:0] incrementer_1_output, multiplexer_1_out;

  Incrementer incrementer_1 (.Input(Output), .Output(incrementer_1_output));
  Multiplexer #(.select(2), .width(10), .enable("false")) multiplexer_1 (
    .in0(Output), .in1(incrementer_1_output), .in2(Input), .in3(Output), .out(multiplexer_1_out),
    .sel({Write_Address, Increment}));
  _10_bit_Load_Register u_10_bit_load_register_1 (
    .Register_Input(multiplexer_1_out), .Write_Enable(1'b1), .Reset(Reset), .Register_Output(Output),
    .Clock(Clock));

  // Notes on the sheet:
  //   keep pc value/increment pc value/write direclty pc
endmodule

module _10_bit_Register (
  input  [9:0] Data_Input,
  input  Clock,
  output [9:0] Data_Output
);

  Flip_Flop ff_1 (.D(Data_Input[0]), .Clk(Clock), .Q(Data_Output[0]));
  Flip_Flop ff_2 (.D(Data_Input[1]), .Clk(Clock), .Q(Data_Output[1]));
  Flip_Flop ff_3 (.D(Data_Input[2]), .Clk(Clock), .Q(Data_Output[2]));
  Flip_Flop ff_4 (.D(Data_Input[3]), .Clk(Clock), .Q(Data_Output[3]));
  Flip_Flop ff_5 (.D(Data_Input[4]), .Clk(Clock), .Q(Data_Output[4]));
  Flip_Flop ff_6 (.D(Data_Input[5]), .Clk(Clock), .Q(Data_Output[5]));
  Flip_Flop ff_7 (.D(Data_Input[6]), .Clk(Clock), .Q(Data_Output[6]));
  Flip_Flop ff_8 (.D(Data_Input[7]), .Clk(Clock), .Q(Data_Output[7]));
  Flip_Flop ff_9 (.D(Data_Input[8]), .Clk(Clock), .Q(Data_Output[8]));
  Flip_Flop ff_10 (.D(Data_Input[9]), .Clk(Clock), .Q(Data_Output[9]));
endmodule

module _10_bit_Load_Register (
  input  [9:0] Register_Input,
  input  Write_Enable,
  input  Reset,
  input  Clock,
  output [9:0] Register_Output
);

  wire [9:0] multiplexer_1_out;

  Multiplexer #(.select(2), .width(10), .enable("false")) multiplexer_1 (
    .in0(Register_Output), .in1(Register_Input), .in2({10{1'b0}}), .in3({10{1'b0}}), .out(multiplexer_1_out),
    .sel({Reset, Write_Enable}));
  _10_bit_Register Register (.Data_Input(multiplexer_1_out), .Clock(Clock), .Data_Output(Register_Output));

  // Notes on the sheet:
  //   reset enable => 10
  //   keep value => 00
  //   write enable => 01
endmodule

module Incrementer (
  input  [9:0] Input,
  output [9:0] Output
);

  wire half_adder_2_carryout, half_adder_3_carryout, half_adder_4_carryout, half_adder_5_carryout,
       half_adder_6_carryout, half_adder_7_carryout, half_adder_8_carryout, half_adder_9_carryout,
       half_adder_10_carryout;

  half_adder half_adder_1 (.B(Input[9]), .A(half_adder_2_carryout), .Sum(Output[9]));  // open: CarryOut
  half_adder half_adder_2 (.B(Input[8]), .A(half_adder_3_carryout), .CarryOut(half_adder_2_carryout), .Sum(Output[8]));
  half_adder half_adder_3 (.B(Input[7]), .A(half_adder_4_carryout), .CarryOut(half_adder_3_carryout), .Sum(Output[7]));
  half_adder half_adder_4 (.B(Input[6]), .A(half_adder_6_carryout), .CarryOut(half_adder_4_carryout), .Sum(Output[6]));
  half_adder half_adder_5 (.B(Input[4]), .A(half_adder_7_carryout), .CarryOut(half_adder_5_carryout), .Sum(Output[4]));
  half_adder half_adder_6 (.B(Input[5]), .A(half_adder_5_carryout), .CarryOut(half_adder_6_carryout), .Sum(Output[5]));
  half_adder half_adder_7 (.B(Input[3]), .A(half_adder_8_carryout), .CarryOut(half_adder_7_carryout), .Sum(Output[3]));
  half_adder half_adder_8 (.B(Input[2]), .A(half_adder_9_carryout), .CarryOut(half_adder_8_carryout), .Sum(Output[2]));
  half_adder half_adder_9 (.B(Input[1]), .A(half_adder_10_carryout), .CarryOut(half_adder_9_carryout), .Sum(Output[1]));
  half_adder half_adder_10 (.B(Input[0]), .A(1'b1), .CarryOut(half_adder_10_carryout), .Sum(Output[0]));
endmodule

module Sign_Extender (
  input  [9:0] _10_bit_Input,
  output [17:0] _18_bit_Input
);

  Multiplexer #(.width(8), .enable("false")) multiplexer_1 (
    .in0({8{1'b0}}), .in1({8{1'b1}}), .out(_18_bit_Input[17:10]), .sel(_10_bit_Input[9]));

  assign _18_bit_Input[9:0] = _10_bit_Input;
endmodule

module Zero_Extender (
  input  [9:0] _10_bit_Input,
  output [17:0] _18_bit_Input
);


  assign _18_bit_Input = {{8{1'b0}}, _10_bit_Input};
endmodule

module Comparator (
  input  A,
  input  B,
  input  in_gt,
  input  in_lt,
  input  in_eq,
  output A_greater_B,
  output A_less_B,
  output A_equal_B
);

  wire and_1_out, and_2_out, not_1_out, xnor_1_out;

  not not_1 (not_1_out, A);
  and and_1 (and_1_out, not_1_out, B, in_eq);
  and and_2 (and_2_out, in_eq, A, ~B);  // AND_Gate
  xnor xnor_1 (xnor_1_out, B, A);
  or or_1 (A_greater_B, in_gt, and_2_out);
  or or_2 (A_less_B, in_lt, and_1_out);
  and and_3 (A_equal_B, in_eq, xnor_1_out);
endmodule

module deneme (
  input  in_1
);


  // Notes on the sheet:
  //   THIS IS FREE AREA, YOU CAN FREELY WORK HERE
endmodule

module Control_Unit (
  input  [17:0] Instruction,
  output Reset,
  output ADD_SIG,
  output [5:0] Immediate,
  output REG_WR,
  output [9:0] Address,
  output [3:0] Last_4_bits,
  output [3:0] Second_4_bits_After_Opcode,
  output [3:0] First_4_bits_After_Opcode
);

  wire decoder_1_out1, decoder_1_out2, decoder_1_out3, decoder_1_out4, decoder_1_out5, decoder_1_out6,
       decoder_1_out7, decoder_1_out8, decoder_1_out9, decoder_1_out10, decoder_1_out11, decoder_1_out12,
       decoder_1_out13, decoder_1_out14, decoder_1_out15;

  Decoder #(.select(4), .enable("false")) decoder_1 (
    .out0(ADD_SIG), .out1(decoder_1_out1), .out2(decoder_1_out2), .out3(decoder_1_out3),
    .out4(decoder_1_out4), .out5(decoder_1_out5), .out6(decoder_1_out6), .out7(decoder_1_out7),
    .out8(decoder_1_out8), .out9(decoder_1_out9), .out10(decoder_1_out10), .out11(decoder_1_out11),
    .out12(decoder_1_out12), .out13(decoder_1_out13), .out14(decoder_1_out14), .out15(decoder_1_out15),
    .sel(Instruction[17:14]));

  assign Address = Instruction[9:0];
  assign First_4_bits_After_Opcode = Instruction[13:10];
  assign Immediate = Instruction[5:0];
  assign Last_4_bits = Instruction[3:0];
  assign REG_WR = ADD_SIG;
  assign Second_4_bits_After_Opcode = Instruction[9:6];

  // Notes on the sheet:
  //   Decode Opcode
endmodule

module Flip_Flop (
  input  D,
  input  Clk,
  output Q
);

  wire d_latch_1_q, not_1_out;

  not not_1 (not_1_out, Clk);
  D_Latch d_latch_1 (.D(D), .Clk(not_1_out), .Q(d_latch_1_q));
  D_Latch d_latch_2 (.D(d_latch_1_q), .Clk(Clk), .Q(Q));
endmodule

module D_Latch (
  input  D,
  input  Clk,
  output Q
);

  wire and_1_out, and_2_out, nor_1_out, not_1_out;

  not not_1 (not_1_out, D);
  and and_1 (and_1_out, D, Clk);
  and and_2 (and_2_out, Clk, not_1_out);
  nor nor_1 (nor_1_out, and_1_out, Q);
  nor nor_2 (Q, nor_1_out, and_2_out);
endmodule

module _18_Bit_Reg (
  input  [17:0] D,
  input  Clk,
  output [17:0] Q
);

  Flip_Flop _0 (.D(D[0]), .Clk(Clk), .Q(Q[0]));
  Flip_Flop _1 (.D(D[1]), .Clk(Clk), .Q(Q[1]));
  Flip_Flop _2 (.D(D[2]), .Clk(Clk), .Q(Q[2]));
  Flip_Flop _3 (.D(D[3]), .Clk(Clk), .Q(Q[3]));
  Flip_Flop _4 (.D(D[4]), .Clk(Clk), .Q(Q[4]));
  Flip_Flop _5 (.D(D[5]), .Clk(Clk), .Q(Q[5]));
  Flip_Flop _6 (.D(D[6]), .Clk(Clk), .Q(Q[6]));
  Flip_Flop _7 (.D(D[7]), .Clk(Clk), .Q(Q[7]));
  Flip_Flop _8 (.D(D[8]), .Clk(Clk), .Q(Q[8]));
  Flip_Flop _9 (.D(D[9]), .Clk(Clk), .Q(Q[9]));
  Flip_Flop _10 (.D(D[10]), .Clk(Clk), .Q(Q[10]));
  Flip_Flop _11 (.D(D[11]), .Clk(Clk), .Q(Q[11]));
  Flip_Flop _12 (.D(D[12]), .Clk(Clk), .Q(Q[12]));
  Flip_Flop _13 (.D(D[13]), .Clk(Clk), .Q(Q[13]));
  Flip_Flop _14 (.D(D[14]), .Clk(Clk), .Q(Q[14]));
  Flip_Flop _15 (.D(D[15]), .Clk(Clk), .Q(Q[15]));
  Flip_Flop _16 (.D(D[16]), .Clk(Clk), .Q(Q[16]));
  Flip_Flop _17 (.D(D[17]), .Clk(Clk), .Q(Q[17]));
endmodule

module Register_File (
  input  Reset,
  input  W_Enabled,
  input  Clock,
  input  [17:0] W_Data,
  input  [3:0] W_Address,
  input  [3:0] R1_Address,
  input  [3:0] R2_Address,
  output [17:0] R1_Data,
  output [17:0] R2_Data
);

  wire decoder_1_out0, decoder_1_out1, decoder_1_out2, decoder_1_out3, decoder_1_out4, decoder_1_out5,
       decoder_1_out6, decoder_1_out7, decoder_1_out8, decoder_1_out9, decoder_1_out10, decoder_1_out11,
       decoder_1_out12, decoder_1_out13, decoder_1_out14, decoder_1_out15, decoder_2_out0, decoder_2_out1,
       decoder_2_out2, decoder_2_out3, decoder_2_out4, decoder_2_out5, decoder_2_out6, decoder_2_out7,
       decoder_2_out8, decoder_2_out9, decoder_2_out10, decoder_2_out11, decoder_2_out12, decoder_2_out13,
       decoder_2_out14, decoder_2_out15, decoder_3_out0, decoder_3_out1, decoder_3_out2, decoder_3_out3,
       decoder_3_out4, decoder_3_out5, decoder_3_out6, decoder_3_out7, decoder_3_out8, decoder_3_out9,
       decoder_3_out10, decoder_3_out11, decoder_3_out12, decoder_3_out13, decoder_3_out14, decoder_3_out15;
  wire [17:0] n18_bit_load_register_1_out_5, n18_bit_load_register_2_out_5, n18_bit_load_register_3_out_5,
       n18_bit_load_register_4_out_5, n18_bit_load_register_5_out_5, n18_bit_load_register_6_out_5,
       n18_bit_load_register_7_out_5, n18_bit_load_register_8_out_5, n18_bit_load_register_9_out_5,
       n18_bit_load_register_10_out_5, n18_bit_load_register_11_out_5, n18_bit_load_register_12_out_5,
       n18_bit_load_register_13_out_5, n18_bit_load_register_14_out_5, n18_bit_load_register_15_out_5,
       n18_bit_load_register_16_out_5;

  Decoder #(.select(4), .disabled(0), .enable("false")) decoder_1 (
    .out0(decoder_1_out0), .out1(decoder_1_out1), .out2(decoder_1_out2), .out3(decoder_1_out3),
    .out4(decoder_1_out4), .out5(decoder_1_out5), .out6(decoder_1_out6), .out7(decoder_1_out7),
    .out8(decoder_1_out8), .out9(decoder_1_out9), .out10(decoder_1_out10), .out11(decoder_1_out11),
    .out12(decoder_1_out12), .out13(decoder_1_out13), .out14(decoder_1_out14), .out15(decoder_1_out15),
    .sel(R1_Address));
  _18_bit_Load_Register u_18_bit_load_register_1 (
    .W_Enable(decoder_2_out0), .Reset(Reset), .out_5(n18_bit_load_register_1_out_5), .Load(W_Data),
    .Clk(Clock));
  _18_bit_Load_Register u_18_bit_load_register_2 (
    .W_Enable(decoder_2_out1), .Reset(Reset), .out_5(n18_bit_load_register_2_out_5), .Load(W_Data),
    .Clk(Clock));
  _18_bit_Load_Register u_18_bit_load_register_3 (
    .W_Enable(decoder_2_out2), .Reset(Reset), .out_5(n18_bit_load_register_3_out_5), .Load(W_Data),
    .Clk(Clock));
  _18_bit_Load_Register u_18_bit_load_register_4 (
    .W_Enable(decoder_2_out3), .Reset(Reset), .out_5(n18_bit_load_register_4_out_5), .Load(W_Data),
    .Clk(Clock));
  _18_bit_Load_Register u_18_bit_load_register_5 (
    .W_Enable(decoder_2_out4), .Reset(Reset), .out_5(n18_bit_load_register_5_out_5), .Load(W_Data),
    .Clk(Clock));
  _18_bit_Load_Register u_18_bit_load_register_6 (
    .W_Enable(decoder_2_out5), .Reset(Reset), .out_5(n18_bit_load_register_6_out_5), .Load(W_Data),
    .Clk(Clock));
  _18_bit_Load_Register u_18_bit_load_register_7 (
    .W_Enable(decoder_2_out6), .Reset(Reset), .out_5(n18_bit_load_register_7_out_5), .Load(W_Data),
    .Clk(Clock));
  _18_bit_Load_Register u_18_bit_load_register_8 (
    .W_Enable(decoder_2_out7), .Reset(Reset), .out_5(n18_bit_load_register_8_out_5), .Load(W_Data),
    .Clk(Clock));
  Decoder #(.select(4), .disabled(0)) decoder_2 (
    .out0(decoder_2_out0), .out1(decoder_2_out1), .out2(decoder_2_out2), .out3(decoder_2_out3),
    .out4(decoder_2_out4), .out5(decoder_2_out5), .out6(decoder_2_out6), .out7(decoder_2_out7),
    .out8(decoder_2_out8), .out9(decoder_2_out9), .out10(decoder_2_out10), .out11(decoder_2_out11),
    .out12(decoder_2_out12), .out13(decoder_2_out13), .out14(decoder_2_out14), .out15(decoder_2_out15),
    .sel(W_Address), .en(W_Enabled));
  assign R1_Data = decoder_1_out0 ? n18_bit_load_register_1_out_5 : 18'bz;  // Controlled_Buffer controlled_buffer_1
  assign R1_Data = decoder_1_out1 ? n18_bit_load_register_2_out_5 : 18'bz;  // Controlled_Buffer controlled_buffer_2
  assign R1_Data = decoder_1_out2 ? n18_bit_load_register_3_out_5 : 18'bz;  // Controlled_Buffer controlled_buffer_3
  assign R1_Data = decoder_1_out3 ? n18_bit_load_register_4_out_5 : 18'bz;  // Controlled_Buffer controlled_buffer_4
  assign R1_Data = decoder_1_out4 ? n18_bit_load_register_5_out_5 : 18'bz;  // Controlled_Buffer controlled_buffer_5
  assign R1_Data = decoder_1_out5 ? n18_bit_load_register_6_out_5 : 18'bz;  // Controlled_Buffer controlled_buffer_6
  assign R1_Data = decoder_1_out6 ? n18_bit_load_register_7_out_5 : 18'bz;  // Controlled_Buffer controlled_buffer_7
  assign R1_Data = decoder_1_out7 ? n18_bit_load_register_8_out_5 : 18'bz;  // Controlled_Buffer controlled_buffer_8
  assign R1_Data = decoder_1_out8 ? n18_bit_load_register_9_out_5 : 18'bz;  // Controlled_Buffer controlled_buffer_9
  assign R1_Data = decoder_1_out9 ? n18_bit_load_register_10_out_5 : 18'bz;  // Controlled_Buffer controlled_buffer_10
  assign R1_Data = decoder_1_out10 ? n18_bit_load_register_11_out_5 : 18'bz;  // Controlled_Buffer controlled_buffer_11
  assign R1_Data = decoder_1_out11 ? n18_bit_load_register_12_out_5 : 18'bz;  // Controlled_Buffer controlled_buffer_12
  assign R1_Data = decoder_1_out12 ? n18_bit_load_register_13_out_5 : 18'bz;  // Controlled_Buffer controlled_buffer_13
  assign R1_Data = decoder_1_out13 ? n18_bit_load_register_14_out_5 : 18'bz;  // Controlled_Buffer controlled_buffer_14
  assign R1_Data = decoder_1_out14 ? n18_bit_load_register_15_out_5 : 18'bz;  // Controlled_Buffer controlled_buffer_15
  _18_bit_Load_Register u_18_bit_load_register_9 (
    .W_Enable(decoder_2_out8), .Reset(Reset), .out_5(n18_bit_load_register_9_out_5), .Load(W_Data),
    .Clk(Clock));
  _18_bit_Load_Register u_18_bit_load_register_10 (
    .W_Enable(decoder_2_out9), .Reset(Reset), .out_5(n18_bit_load_register_10_out_5), .Load(W_Data),
    .Clk(Clock));
  _18_bit_Load_Register u_18_bit_load_register_11 (
    .W_Enable(decoder_2_out10), .Reset(Reset), .out_5(n18_bit_load_register_11_out_5), .Load(W_Data),
    .Clk(Clock));
  _18_bit_Load_Register u_18_bit_load_register_12 (
    .W_Enable(decoder_2_out11), .Reset(Reset), .out_5(n18_bit_load_register_12_out_5), .Load(W_Data),
    .Clk(Clock));
  _18_bit_Load_Register u_18_bit_load_register_13 (
    .W_Enable(decoder_2_out12), .Reset(Reset), .out_5(n18_bit_load_register_13_out_5), .Load(W_Data),
    .Clk(Clock));
  _18_bit_Load_Register u_18_bit_load_register_14 (
    .W_Enable(decoder_2_out13), .Reset(Reset), .out_5(n18_bit_load_register_14_out_5), .Load(W_Data),
    .Clk(Clock));
  _18_bit_Load_Register u_18_bit_load_register_15 (
    .W_Enable(decoder_2_out14), .Reset(Reset), .out_5(n18_bit_load_register_15_out_5), .Load(W_Data),
    .Clk(Clock));
  _18_bit_Load_Register u_18_bit_load_register_16 (
    .W_Enable(decoder_2_out15), .Reset(Reset), .out_5(n18_bit_load_register_16_out_5), .Load(W_Data),
    .Clk(Clock));
  assign R1_Data = decoder_1_out15 ? n18_bit_load_register_16_out_5 : 18'bz;  // Controlled_Buffer controlled_buffer_16
  Decoder #(.select(4), .disabled(0), .enable("false")) decoder_3 (
    .out0(decoder_3_out0), .out1(decoder_3_out1), .out2(decoder_3_out2), .out3(decoder_3_out3),
    .out4(decoder_3_out4), .out5(decoder_3_out5), .out6(decoder_3_out6), .out7(decoder_3_out7),
    .out8(decoder_3_out8), .out9(decoder_3_out9), .out10(decoder_3_out10), .out11(decoder_3_out11),
    .out12(decoder_3_out12), .out13(decoder_3_out13), .out14(decoder_3_out14), .out15(decoder_3_out15),
    .sel(R2_Address));
  assign R2_Data = decoder_3_out0 ? n18_bit_load_register_1_out_5 : 18'bz;  // Controlled_Buffer controlled_buffer_17
  assign R2_Data = decoder_3_out1 ? n18_bit_load_register_2_out_5 : 18'bz;  // Controlled_Buffer controlled_buffer_18
  assign R2_Data = decoder_3_out2 ? n18_bit_load_register_3_out_5 : 18'bz;  // Controlled_Buffer controlled_buffer_19
  assign R2_Data = decoder_3_out3 ? n18_bit_load_register_4_out_5 : 18'bz;  // Controlled_Buffer controlled_buffer_20
  assign R2_Data = decoder_3_out4 ? n18_bit_load_register_5_out_5 : 18'bz;  // Controlled_Buffer controlled_buffer_21
  assign R2_Data = decoder_3_out5 ? n18_bit_load_register_6_out_5 : 18'bz;  // Controlled_Buffer controlled_buffer_22
  assign R2_Data = decoder_3_out6 ? n18_bit_load_register_7_out_5 : 18'bz;  // Controlled_Buffer controlled_buffer_23
  assign R2_Data = decoder_3_out7 ? n18_bit_load_register_8_out_5 : 18'bz;  // Controlled_Buffer controlled_buffer_24
  assign R2_Data = decoder_3_out8 ? n18_bit_load_register_9_out_5 : 18'bz;  // Controlled_Buffer controlled_buffer_25
  assign R2_Data = decoder_3_out9 ? n18_bit_load_register_10_out_5 : 18'bz;  // Controlled_Buffer controlled_buffer_26
  assign R2_Data = decoder_3_out10 ? n18_bit_load_register_11_out_5 : 18'bz;  // Controlled_Buffer controlled_buffer_27
  assign R2_Data = decoder_3_out11 ? n18_bit_load_register_12_out_5 : 18'bz;  // Controlled_Buffer controlled_buffer_28
  assign R2_Data = decoder_3_out12 ? n18_bit_load_register_13_out_5 : 18'bz;  // Controlled_Buffer controlled_buffer_29
  assign R2_Data = decoder_3_out13 ? n18_bit_load_register_14_out_5 : 18'bz;  // Controlled_Buffer controlled_buffer_30
  assign R2_Data = decoder_3_out14 ? n18_bit_load_register_15_out_5 : 18'bz;  // Controlled_Buffer controlled_buffer_31
  assign R2_Data = decoder_3_out15 ? n18_bit_load_register_16_out_5 : 18'bz;  // Controlled_Buffer controlled_buffer_32
endmodule

module _18_bit_Load_Register (
  input  [17:0] Load,
  input  Clk,
  input  W_Enable,
  input  Reset,
  output [17:0] out_5
);

  wire [17:0] multiplexer_1_out;

  Multiplexer #(.select(2), .width(18), .enable("false")) multiplexer_1 (
    .in0(out_5), .in1(Load), .in2({18{1'b0}}), .in3({18{1'b0}}), .out(multiplexer_1_out),
    .sel({Reset, W_Enable}));
  _18_Bit_Reg u_18_bit_reg_1 (.D(multiplexer_1_out), .Clk(Clk), .Q(out_5));
endmodule

module half_adder (
  input  B,
  input  A,
  output CarryOut,
  output Sum
);

  and and_1 (CarryOut, B, A);
  xor xor_1 (Sum, B, A);
endmodule

module full_adder (
  input  B,
  input  A,
  input  Carry_in,
  output CarryOut,
  output Sum
);

  wire and_1_out, and_2_out, and_3_out;

  and and_1 (and_1_out, B, A);
  and and_2 (and_2_out, B, Carry_in);
  or or_1 (CarryOut, and_1_out, and_2_out, and_3_out);
  and and_3 (and_3_out, A, Carry_in);
  ExactlyOne xor_1 (.out(Sum), .in0(B), .in1(A), .in2(Carry_in));
endmodule

// Add
module Adder (
  input  [17:0] B,
  input  [17:0] A,
  output [17:0] Out
);

  wire full_adder_1_carryout, full_adder_2_carryout, full_adder_4_carryout, full_adder_5_carryout,
       full_adder_6_carryout, full_adder_7_carryout, full_adder_8_carryout, full_adder_9_carryout,
       full_adder_10_carryout, full_adder_11_carryout, full_adder_12_carryout, full_adder_13_carryout,
       full_adder_14_carryout, full_adder_15_carryout, full_adder_16_carryout, full_adder_17_carryout,
       half_adder_1_carryout;

  full_adder full_adder_1 (
    .B(B[15]), .A(A[15]), .Carry_in(full_adder_7_carryout), .CarryOut(full_adder_1_carryout), .Sum(Out[15]));
  full_adder full_adder_2 (
    .B(B[16]), .A(A[16]), .Carry_in(full_adder_1_carryout), .CarryOut(full_adder_2_carryout), .Sum(Out[16]));
  full_adder full_adder_3 (.B(B[17]), .A(A[17]), .Carry_in(full_adder_2_carryout), .Sum(Out[17]));  // open: CarryOut
  full_adder full_adder_4 (
    .B(B[11]), .A(A[11]), .Carry_in(full_adder_11_carryout), .CarryOut(full_adder_4_carryout), .Sum(Out[11]));
  full_adder full_adder_5 (
    .B(B[12]), .A(A[12]), .Carry_in(full_adder_4_carryout), .CarryOut(full_adder_5_carryout), .Sum(Out[12]));
  full_adder full_adder_6 (
    .B(B[13]), .A(A[13]), .Carry_in(full_adder_5_carryout), .CarryOut(full_adder_6_carryout), .Sum(Out[13]));
  full_adder full_adder_7 (
    .B(B[14]), .A(A[14]), .Carry_in(full_adder_6_carryout), .CarryOut(full_adder_7_carryout), .Sum(Out[14]));
  full_adder full_adder_8 (
    .B(B[7]), .A(A[7]), .Carry_in(full_adder_15_carryout), .CarryOut(full_adder_8_carryout), .Sum(Out[7]));
  full_adder full_adder_9 (
    .B(B[8]), .A(A[8]), .Carry_in(full_adder_8_carryout), .CarryOut(full_adder_9_carryout), .Sum(Out[8]));
  full_adder full_adder_10 (
    .B(B[9]), .A(A[9]), .Carry_in(full_adder_9_carryout), .CarryOut(full_adder_10_carryout), .Sum(Out[9]));
  full_adder full_adder_11 (
    .B(B[10]), .A(A[10]), .Carry_in(full_adder_10_carryout), .CarryOut(full_adder_11_carryout), .Sum(Out[10]));
  full_adder full_adder_12 (
    .B(B[3]), .A(A[3]), .Carry_in(full_adder_17_carryout), .CarryOut(full_adder_12_carryout), .Sum(Out[3]));
  full_adder full_adder_13 (
    .B(B[4]), .A(A[4]), .Carry_in(full_adder_12_carryout), .CarryOut(full_adder_13_carryout), .Sum(Out[4]));
  full_adder full_adder_14 (
    .B(B[5]), .A(A[5]), .Carry_in(full_adder_13_carryout), .CarryOut(full_adder_14_carryout), .Sum(Out[5]));
  full_adder full_adder_15 (
    .B(B[6]), .A(A[6]), .Carry_in(full_adder_14_carryout), .CarryOut(full_adder_15_carryout), .Sum(Out[6]));
  half_adder half_adder_1 (.B(B[0]), .A(A[0]), .CarryOut(half_adder_1_carryout), .Sum(Out[0]));
  full_adder full_adder_16 (
    .B(B[1]), .A(A[1]), .Carry_in(half_adder_1_carryout), .CarryOut(full_adder_16_carryout), .Sum(Out[1]));
  full_adder full_adder_17 (
    .B(B[2]), .A(A[2]), .Carry_in(full_adder_16_carryout), .CarryOut(full_adder_17_carryout), .Sum(Out[2]));
endmodule

module And (
  input  [17:0] A,
  input  [17:0] B,
  output [17:0] Out
);

  assign Out = A & B;  // AND_Gate and_1, 18 bits wide
endmodule

module Nand (
  input  [17:0] A,
  input  [17:0] B,
  output [17:0] Out
);

  wire [17:0] and_1_out;

  assign and_1_out = A & B;  // AND_Gate and_1, 18 bits wide
  assign Out = ~and_1_out;  // NOT_Gate not_1, 18 bits wide
endmodule

module Nor (
  input  [17:0] A,
  input  [17:0] B,
  output [17:0] Out
);

  wire [17:0] or_1_out;

  assign or_1_out = A | B;  // OR_Gate or_1, 18 bits wide
  assign Out = ~or_1_out;  // NOT_Gate not_1, 18 bits wide
endmodule

module ALU (
  input  [17:0] A,
  input  [17:0] B,
  input  ADD,
  input  AND,
  input  NAND,
  input  NOR,
  output [17:0] Out
);

  wire [17:0] adder_1_out, and_1_out, nand_1_out, nor_1_out;

  And and_1 (.A(A), .B(B), .Out(and_1_out));
  Adder adder_1 (.B(B), .A(A), .Out(adder_1_out));
  assign Out = ADD ? adder_1_out : 18'bz;  // Controlled_Buffer controlled_buffer_1
  assign Out = AND ? and_1_out : 18'bz;  // Controlled_Buffer controlled_buffer_2
  Nand nand_1 (.A(A), .B(B), .Out(nand_1_out));
  Nor nor_1 (.A(A), .B(B), .Out(nor_1_out));
  assign Out = NAND ? nand_1_out : 18'bz;  // Controlled_Buffer controlled_buffer_3
  assign Out = NOR ? nor_1_out : 18'bz;  // Controlled_Buffer controlled_buffer_4
endmodule

module \_1bıt_magnitude_comparator  (
  input  a,
  input  i_gt,
  input  i_eq,
  input  i_lt,
  input  b,
  output o_gt,
  output o_eq,
  output o_lt
);

  wire and_1_out, and_2_out, not_1_out, not_2_out, xnor_1_out;

  not not_1 (not_1_out, b);
  not not_2 (not_2_out, a);
  and and_1 (and_1_out, a, i_eq, not_1_out);
  xnor xnor_1 (xnor_1_out, a, b);
  and and_2 (and_2_out, not_2_out, i_eq, b);
  or or_1 (o_gt, i_gt, and_1_out);
  and and_3 (o_eq, i_eq, xnor_1_out);
  or or_2 (o_lt, i_lt, and_2_out);
endmodule

module _18bit_magnitude_comparator (
  input  [17:0] a,
  input  [17:0] b,
  output out_3,
  output out_4,
  output out_5
);

  wire \n1bıt_magnitude_comparator_1_o_eq , \n1bıt_magnitude_comparator_1_o_gt ,
       \n1bıt_magnitude_comparator_1_o_lt , \n1bıt_magnitude_comparator_2_o_eq ,
       \n1bıt_magnitude_comparator_2_o_gt , \n1bıt_magnitude_comparator_2_o_lt ,
       \n1bıt_magnitude_comparator_3_o_eq , \n1bıt_magnitude_comparator_3_o_gt ,
       \n1bıt_magnitude_comparator_3_o_lt , \n1bıt_magnitude_comparator_4_o_eq ,
       \n1bıt_magnitude_comparator_4_o_gt , \n1bıt_magnitude_comparator_4_o_lt ,
       \n1bıt_magnitude_comparator_5_o_eq , \n1bıt_magnitude_comparator_5_o_gt ,
       \n1bıt_magnitude_comparator_5_o_lt , \n1bıt_magnitude_comparator_6_o_eq ,
       \n1bıt_magnitude_comparator_6_o_gt , \n1bıt_magnitude_comparator_6_o_lt ,
       \n1bıt_magnitude_comparator_7_o_eq , \n1bıt_magnitude_comparator_7_o_gt ,
       \n1bıt_magnitude_comparator_7_o_lt , \n1bıt_magnitude_comparator_8_o_eq ,
       \n1bıt_magnitude_comparator_8_o_gt , \n1bıt_magnitude_comparator_8_o_lt ,
       \n1bıt_magnitude_comparator_9_o_eq , \n1bıt_magnitude_comparator_9_o_gt ,
       \n1bıt_magnitude_comparator_9_o_lt , \n1bıt_magnitude_comparator_10_o_eq ,
       \n1bıt_magnitude_comparator_10_o_gt , \n1bıt_magnitude_comparator_10_o_lt ,
       \n1bıt_magnitude_comparator_11_o_eq , \n1bıt_magnitude_comparator_11_o_gt ,
       \n1bıt_magnitude_comparator_11_o_lt , \n1bıt_magnitude_comparator_12_o_eq ,
       \n1bıt_magnitude_comparator_12_o_gt , \n1bıt_magnitude_comparator_12_o_lt ,
       \n1bıt_magnitude_comparator_13_o_eq , \n1bıt_magnitude_comparator_13_o_gt ,
       \n1bıt_magnitude_comparator_13_o_lt , \n1bıt_magnitude_comparator_14_o_eq ,
       \n1bıt_magnitude_comparator_14_o_gt , \n1bıt_magnitude_comparator_14_o_lt ,
       \n1bıt_magnitude_comparator_15_o_eq , \n1bıt_magnitude_comparator_15_o_gt ,
       \n1bıt_magnitude_comparator_15_o_lt , \n1bıt_magnitude_comparator_16_o_eq ,
       \n1bıt_magnitude_comparator_16_o_gt , \n1bıt_magnitude_comparator_16_o_lt ,
       \n1bıt_magnitude_comparator_17_o_eq , \n1bıt_magnitude_comparator_17_o_gt ,
       \n1bıt_magnitude_comparator_17_o_lt ;

  \_1bıt_magnitude_comparator  \u_1bıt_magnitude_comparator_1  (
    .i_gt(1'b0), .i_eq(1'b1), .i_lt(1'b0), .a(a[17]), .b(b[17]), .o_gt(\n1bıt_magnitude_comparator_1_o_gt ),
    .o_eq(\n1bıt_magnitude_comparator_1_o_eq ), .o_lt(\n1bıt_magnitude_comparator_1_o_lt ));
  \_1bıt_magnitude_comparator  \u_1bıt_magnitude_comparator_2  (
    .i_gt(\n1bıt_magnitude_comparator_3_o_gt ), .i_eq(\n1bıt_magnitude_comparator_3_o_eq ),
    .i_lt(\n1bıt_magnitude_comparator_3_o_lt ), .a(a[15]), .b(b[15]),
    .o_gt(\n1bıt_magnitude_comparator_2_o_gt ), .o_eq(\n1bıt_magnitude_comparator_2_o_eq ),
    .o_lt(\n1bıt_magnitude_comparator_2_o_lt ));
  \_1bıt_magnitude_comparator  \u_1bıt_magnitude_comparator_3  (
    .i_gt(\n1bıt_magnitude_comparator_1_o_gt ), .i_eq(\n1bıt_magnitude_comparator_1_o_eq ),
    .i_lt(\n1bıt_magnitude_comparator_1_o_lt ), .a(a[16]), .b(b[16]),
    .o_gt(\n1bıt_magnitude_comparator_3_o_gt ), .o_eq(\n1bıt_magnitude_comparator_3_o_eq ),
    .o_lt(\n1bıt_magnitude_comparator_3_o_lt ));
  \_1bıt_magnitude_comparator  \u_1bıt_magnitude_comparator_4  (
    .i_gt(\n1bıt_magnitude_comparator_2_o_gt ), .i_eq(\n1bıt_magnitude_comparator_2_o_eq ),
    .i_lt(\n1bıt_magnitude_comparator_2_o_lt ), .a(a[14]), .b(b[14]),
    .o_gt(\n1bıt_magnitude_comparator_4_o_gt ), .o_eq(\n1bıt_magnitude_comparator_4_o_eq ),
    .o_lt(\n1bıt_magnitude_comparator_4_o_lt ));
  \_1bıt_magnitude_comparator  \u_1bıt_magnitude_comparator_5  (
    .i_gt(\n1bıt_magnitude_comparator_4_o_gt ), .i_eq(\n1bıt_magnitude_comparator_4_o_eq ),
    .i_lt(\n1bıt_magnitude_comparator_4_o_lt ), .a(a[13]), .b(b[13]),
    .o_gt(\n1bıt_magnitude_comparator_5_o_gt ), .o_eq(\n1bıt_magnitude_comparator_5_o_eq ),
    .o_lt(\n1bıt_magnitude_comparator_5_o_lt ));
  \_1bıt_magnitude_comparator  \u_1bıt_magnitude_comparator_6  (
    .i_gt(\n1bıt_magnitude_comparator_7_o_gt ), .i_eq(\n1bıt_magnitude_comparator_7_o_eq ),
    .i_lt(\n1bıt_magnitude_comparator_7_o_lt ), .a(a[11]), .b(b[11]),
    .o_gt(\n1bıt_magnitude_comparator_6_o_gt ), .o_eq(\n1bıt_magnitude_comparator_6_o_eq ),
    .o_lt(\n1bıt_magnitude_comparator_6_o_lt ));
  \_1bıt_magnitude_comparator  \u_1bıt_magnitude_comparator_7  (
    .i_gt(\n1bıt_magnitude_comparator_5_o_gt ), .i_eq(\n1bıt_magnitude_comparator_5_o_eq ),
    .i_lt(\n1bıt_magnitude_comparator_5_o_lt ), .a(a[12]), .b(b[12]),
    .o_gt(\n1bıt_magnitude_comparator_7_o_gt ), .o_eq(\n1bıt_magnitude_comparator_7_o_eq ),
    .o_lt(\n1bıt_magnitude_comparator_7_o_lt ));
  \_1bıt_magnitude_comparator  \u_1bıt_magnitude_comparator_8  (
    .i_gt(\n1bıt_magnitude_comparator_6_o_gt ), .i_eq(\n1bıt_magnitude_comparator_6_o_eq ),
    .i_lt(\n1bıt_magnitude_comparator_6_o_lt ), .a(a[10]), .b(b[10]),
    .o_gt(\n1bıt_magnitude_comparator_8_o_gt ), .o_eq(\n1bıt_magnitude_comparator_8_o_eq ),
    .o_lt(\n1bıt_magnitude_comparator_8_o_lt ));
  \_1bıt_magnitude_comparator  \u_1bıt_magnitude_comparator_9  (
    .i_gt(\n1bıt_magnitude_comparator_8_o_gt ), .i_eq(\n1bıt_magnitude_comparator_8_o_eq ),
    .i_lt(\n1bıt_magnitude_comparator_8_o_lt ), .a(a[9]), .b(b[9]),
    .o_gt(\n1bıt_magnitude_comparator_9_o_gt ), .o_eq(\n1bıt_magnitude_comparator_9_o_eq ),
    .o_lt(\n1bıt_magnitude_comparator_9_o_lt ));
  \_1bıt_magnitude_comparator  \u_1bıt_magnitude_comparator_10  (
    .i_gt(\n1bıt_magnitude_comparator_9_o_gt ), .i_eq(\n1bıt_magnitude_comparator_9_o_eq ),
    .i_lt(\n1bıt_magnitude_comparator_9_o_lt ), .a(a[8]), .b(b[8]),
    .o_gt(\n1bıt_magnitude_comparator_10_o_gt ), .o_eq(\n1bıt_magnitude_comparator_10_o_eq ),
    .o_lt(\n1bıt_magnitude_comparator_10_o_lt ));
  \_1bıt_magnitude_comparator  \u_1bıt_magnitude_comparator_11  (
    .i_gt(\n1bıt_magnitude_comparator_10_o_gt ), .i_eq(\n1bıt_magnitude_comparator_10_o_eq ),
    .i_lt(\n1bıt_magnitude_comparator_10_o_lt ), .a(a[7]), .b(b[7]),
    .o_gt(\n1bıt_magnitude_comparator_11_o_gt ), .o_eq(\n1bıt_magnitude_comparator_11_o_eq ),
    .o_lt(\n1bıt_magnitude_comparator_11_o_lt ));
  \_1bıt_magnitude_comparator  \u_1bıt_magnitude_comparator_12  (
    .i_gt(\n1bıt_magnitude_comparator_11_o_gt ), .i_eq(\n1bıt_magnitude_comparator_11_o_eq ),
    .i_lt(\n1bıt_magnitude_comparator_11_o_lt ), .a(a[6]), .b(b[6]),
    .o_gt(\n1bıt_magnitude_comparator_12_o_gt ), .o_eq(\n1bıt_magnitude_comparator_12_o_eq ),
    .o_lt(\n1bıt_magnitude_comparator_12_o_lt ));
  \_1bıt_magnitude_comparator  \u_1bıt_magnitude_comparator_13  (
    .i_gt(\n1bıt_magnitude_comparator_12_o_gt ), .i_eq(\n1bıt_magnitude_comparator_12_o_eq ),
    .i_lt(\n1bıt_magnitude_comparator_12_o_lt ), .a(a[5]), .b(b[5]),
    .o_gt(\n1bıt_magnitude_comparator_13_o_gt ), .o_eq(\n1bıt_magnitude_comparator_13_o_eq ),
    .o_lt(\n1bıt_magnitude_comparator_13_o_lt ));
  \_1bıt_magnitude_comparator  \u_1bıt_magnitude_comparator_14  (
    .i_gt(\n1bıt_magnitude_comparator_13_o_gt ), .i_eq(\n1bıt_magnitude_comparator_13_o_eq ),
    .i_lt(\n1bıt_magnitude_comparator_13_o_lt ), .a(a[4]), .b(b[4]),
    .o_gt(\n1bıt_magnitude_comparator_14_o_gt ), .o_eq(\n1bıt_magnitude_comparator_14_o_eq ),
    .o_lt(\n1bıt_magnitude_comparator_14_o_lt ));
  \_1bıt_magnitude_comparator  \u_1bıt_magnitude_comparator_15  (
    .i_gt(\n1bıt_magnitude_comparator_14_o_gt ), .i_eq(\n1bıt_magnitude_comparator_14_o_eq ),
    .i_lt(\n1bıt_magnitude_comparator_14_o_lt ), .a(a[3]), .b(b[3]),
    .o_gt(\n1bıt_magnitude_comparator_15_o_gt ), .o_eq(\n1bıt_magnitude_comparator_15_o_eq ),
    .o_lt(\n1bıt_magnitude_comparator_15_o_lt ));
  \_1bıt_magnitude_comparator  \u_1bıt_magnitude_comparator_16  (
    .i_gt(\n1bıt_magnitude_comparator_15_o_gt ), .i_eq(\n1bıt_magnitude_comparator_15_o_eq ),
    .i_lt(\n1bıt_magnitude_comparator_15_o_lt ), .a(a[2]), .b(b[2]),
    .o_gt(\n1bıt_magnitude_comparator_16_o_gt ), .o_eq(\n1bıt_magnitude_comparator_16_o_eq ),
    .o_lt(\n1bıt_magnitude_comparator_16_o_lt ));
  \_1bıt_magnitude_comparator  \u_1bıt_magnitude_comparator_17  (
    .i_gt(\n1bıt_magnitude_comparator_16_o_gt ), .i_eq(\n1bıt_magnitude_comparator_16_o_eq ),
    .i_lt(\n1bıt_magnitude_comparator_16_o_lt ), .a(a[1]), .b(b[1]),
    .o_gt(\n1bıt_magnitude_comparator_17_o_gt ), .o_eq(\n1bıt_magnitude_comparator_17_o_eq ),
    .o_lt(\n1bıt_magnitude_comparator_17_o_lt ));
  \_1bıt_magnitude_comparator  \u_1bıt_magnitude_comparator_18  (
    .i_gt(\n1bıt_magnitude_comparator_17_o_gt ), .i_eq(\n1bıt_magnitude_comparator_17_o_eq ),
    .i_lt(\n1bıt_magnitude_comparator_17_o_lt ), .a(a[0]), .b(b[0]), .o_gt(out_3), .o_eq(out_4), .o_lt(out_5));
endmodule

module main_Yusuf (
  input  [17:0] in_1,
  input  [9:0] Address_to_Jump,
  input  in_3,
  input  in_4,
  input  in_5,
  output [9:0] PC_Output,
  output [17:0] INSTRUCTION
);

  wire clock_1_out, control_unit_1_add_sig, control_unit_1_reg_wr, undriven;
  wire [3:0] control_unit_1_first_4_bits_after_opcode, control_unit_1_last_4_bits,
       control_unit_1_second_4_bits_after_opcode;
  wire [5:0] control_unit_1_immediate;
  wire [17:0] alu_1_out, multiplexer_1_out, register_file_1_r1_data, register_file_1_r2_data,
       sign_extender_1__18_bit_input;

  Clock clock_1 (.out(clock_1_out));
  Control_Unit control_unit_1 (
    .Instruction(INSTRUCTION), .First_4_bits_After_Opcode(control_unit_1_first_4_bits_after_opcode),
    .Last_4_bits(control_unit_1_last_4_bits),
    .Second_4_bits_After_Opcode(control_unit_1_second_4_bits_after_opcode),
    .Immediate(control_unit_1_immediate), .ADD_SIG(control_unit_1_add_sig), .REG_WR(control_unit_1_reg_wr));  // open: Address, Reset
  Program_Counter program_counter_1 (
    .Input(Address_to_Jump), .Increment(in_3), .Write_Address(in_4), .Output(PC_Output), .Reset(in_5),
    .Clock(clock_1_out));
  Sign_Extender sign_extender_1 (._18_bit_Input(sign_extender_1__18_bit_input));  // open: _10_bit_Input
  RAM #(.addrWidth(10), .dataWidth(18)) ram_1 (
    .addr(PC_Output), .data(INSTRUCTION), .sel(1'b1), .clk(clock_1_out), .ld(1'b1));  // open: clr
  Register_File register_file_1 (
    .W_Data(alu_1_out), .W_Address(control_unit_1_first_4_bits_after_opcode), .Reset(in_5),
    .R1_Data(register_file_1_r1_data), .Clock(clock_1_out), .W_Enabled(control_unit_1_reg_wr),
    .R2_Data(register_file_1_r2_data), .R2_Address(control_unit_1_second_4_bits_after_opcode),
    .R1_Address(control_unit_1_last_4_bits));
  Multiplexer #(.width(18), .enable("false")) multiplexer_1 (
    .in0(register_file_1_r2_data), .in1(sign_extender_1__18_bit_input), .out(multiplexer_1_out),
    .sel(undriven));
  ALU alu_1 (
    .ADD(control_unit_1_add_sig), .AND(1'b0), .NAND(1'b0), .NOR(1'b0), .A(register_file_1_r1_data),
    .B(multiplexer_1_out), .Out(alu_1_out));

  // Notes on the sheet:
  //   Store ? Load 
  //   RAM
  //   Careful: To get the first 4 bits of instuction, you have to get bits: 17,16,15,14
endmodule
