// Logisim project Processorburak0115.circ as structural Verilog: 35 circuits, main circuit main
module main (
  input  [9:0] Address_to_Jump,
  input  in_2,
  output [9:0] PC_Output,
  output [17:0] INSTRUCTION
);

  wire clock_1_out, CMP_o_eql, CMP_o_lt, control_unit_1_p9, control_unit_1_p10, control_unit_1_p11,
       control_unit_1_p12, control_unit_1_p13, control_unit_1_p14, control_unit_1_p15, flag_file_1_c_out,
       flag_file_1_z_out, not_1_out;
  wire [3:0] control_unit_1_p5, control_unit_1_p6, control_unit_1_p7;
  wire [9:0] control_unit_1_p8, undriven;
  wire [17:0] multiplexer_1_out, multiplexer_2_out, multiplexer_3_out, register_file_1_r1_data,
       register_file_1_r2_data, sign_extender_1__18_bit_input, sign_extender_2__18_bit_input,
       sign_extender_3__18_bit_input;
  wire [17:10] alu_1_out;

  not not_1 (not_1_out, control_unit_1_p13);
  Flag_File flag_file_1 (
    .Write_Enable(control_unit_1_p14), .Reset(control_unit_1_p9), .Clk(clock_1_out), .C_IN(CMP_o_lt),
    .Z_IN(CMP_o_eql), .C_OUT(flag_file_1_c_out), .Z_OUT(flag_file_1_z_out));
  Clock clock_1 (.out(clock_1_out));
  Program_Counter program_counter_1 (
    .Input(Address_to_Jump), .Increment(not_1_out), .Write_Address(control_unit_1_p13), .Output(PC_Output),
    .Reset(in_2), .Clock(clock_1_out));
  // Control_Unit control_unit_1: pin names not known; wires that end beside it: INSTRUCTION, clock_1_out, flag_file_1_z_out, flag_file_1_c_out, control_unit_1_p5, control_unit_1_p6, control_unit_1_p7, control_unit_1_p8, control_unit_1_p9, control_unit_1_p10, control_unit_1_p11, control_unit_1_p12, control_unit_1_p13, control_unit_1_p14, control_unit_1_p15, clock_1_out
  Sign_Extender sign_extender_1 (._10_bit_Input(undriven), ._18_bit_Input(sign_extender_1__18_bit_input));
  Sign_Extender sign_extender_2 (._10_bit_Input(control_unit_1_p8), ._18_bit_Input(sign_extender_2__18_bit_input));
  RAM #(.addrWidth(10), .dataWidth(18)) ram_1 (
    .addr(PC_Output), .data(INSTRUCTION), .sel(1'b1), .ld(1'b1));  // open: clk, clr
  Register_File register_file_1 (
    .W_Data({alu_1_out, Address_to_Jump}), .W_Address(control_unit_1_p5), .Reset(in_2),
    .R1_Data(register_file_1_r1_data), .Clock(clock_1_out), .W_Enabled(control_unit_1_p11),
    .R2_Data(register_file_1_r2_data), .R2_Address(control_unit_1_p7), .R1_Address(control_unit_1_p6));
  Sign_Extender sign_extender_3 (._10_bit_Input(PC_Output), ._18_bit_Input(sign_extender_3__18_bit_input));
  _18bit_magnitude_comparator CMP (
    .a(register_file_1_r2_data), .b(register_file_1_r1_data), .O_EQL(CMP_o_eql), .O_LT(CMP_o_lt));  // open: O_GRT
  Multiplexer #(.width(18), .enable("false")) multiplexer_1 (
    .in0(register_file_1_r1_data), .in1(sign_extender_3__18_bit_input), .out(multiplexer_1_out),
    .sel(control_unit_1_p13));
  Multiplexer #(.width(18), .enable("false")) multiplexer_2 (
    .in0(sign_extender_1__18_bit_input), .in1(sign_extender_2__18_bit_input), .out(multiplexer_2_out),
    .sel(control_unit_1_p13));
  Multiplexer #(.width(18), .enable("false")) multiplexer_3 (
    .in0(register_file_1_r2_data), .in1(multiplexer_2_out), .out(multiplexer_3_out), .sel(control_unit_1_p12));
  ALU alu_1 (
    .ADD(control_unit_1_p10), .AND(1'b0), .NAND(1'b0), .NOR(1'b0), .A(multiplexer_1_out),
    .B(multiplexer_3_out), .Out({alu_1_out, Address_to_Jump}));

  // Notes on the sheet:
  //   RAM
  //   Careful: To get the first 4 bits of instuction, you have to get bits: 17,16,15,14
endmodule

module JE (
  input  ZF,
  input  CF,
  output writeADDR
);

  wire not_1_out;

  not not_1 (not_1_out, CF);
  and and_1 (writeADDR, ZF, not_1_out);
endmodule

module JA (
  input  ZF,
  input  CF,
  output writeADDR
);

  wire not_1_out, not_2_out;

  not not_1 (not_1_out, ZF);
  not not_2 (not_2_out, CF);
  and and_1 (writeADDR, not_1_out, not_2_out);
endmodule

module JB (
  input  ZF,
  input  CF,
  output writeADDR
);

  wire not_1_out;

  not not_1 (not_1_out, ZF);
  and and_1 (writeADDR, not_1_out, CF);
endmodule

module JAE (
  input  CF,
  output writeADDR
);

  not not_1 (writeADDR, CF);
endmodule

module JBE (
  input  ZF,
  input  CF,
  output writeADDR
);

  and and_1 (writeADDR, ZF, CF);
endmodule

module Program_Counter (
  input  [9:0] Input,
  input  Increment,
  input  Clock,
  input  Write_Address,
  input  Reset,
  output [9:0] Output
);

  wire [9:0] incrementer_1_output, multiplexer_1_out;

  Incrementer incrementer_1 (.Input(Output), .Output(incrementer_1_output));
  Multiplexer #(.select(2), .width(10), .enable("false")) multiplexer_1 (
    .in0(Output), .in1(incrementer_1_output), .in2(Input), .in3(Output), .out(multiplexer_1_out),
    .sel({Write_Address, Increment}));
  _10_bit_Load_Register u_10_bit_load_register_1 (
    .Register_Input(multiplexer_1_out), .Write_Enable(1'b1), .Reset(Reset), .Register_Output(Output),
    .Clock(Clock));

  // Notes on the sheet:
  //   keep pc value/increment pc value/write direclty pc
endmodule

module _10_bit_Register (
  input  [9:0] Data_Input,
  input  Clock,
  output [9:0] Data_Output
);

  Flip_Flop ff_1 (.D(Data_Input[0]), .Clk(Clock), .Q(Data_Output[0]));
  Flip_Flop ff_2 (.D(Data_Input[1]), .Clk(Clock), .Q(Data_Output[1]));
  Flip_Flop ff_3 (.D(Data_Input[2]), .Clk(Clock), .Q(Data_Output[2]));
  Flip_Flop ff_4 (.D(Data_Input[3]), .Clk(Clock), .Q(Data_Output[3]));
  Flip_Flop ff_5 (.D(Data_Input[4]), .Clk(Clock), .Q(Data_Output[4]));
  Flip_Flop ff_6 (.D(Data_Input[5]), .Clk(Clock), .Q(Data_Output[5]));
  Flip_Flop ff_7 (.D(Data_Input[6]), .Clk(Clock), .Q(Data_Output[6]));
  Flip_Flop ff_8 (.D(Data_Input[7]), .Clk(Clock), .Q(Data_Output[7]));
  Flip_Flop ff_9 (.D(Data_Input[8]), .Clk(Clock), .Q(Data_Output[8]));
  Flip_Flop ff_10 (.D(Data_Input[9]), .Clk(Clock), .Q(Data_Output[9]));
endmodule

module _10_bit_Load_Register (
  input  [9:0] Register_Input,
  input  Write_Enable,
  input  Reset,
  input  Clock,
  output [9:0] Register_Output
);

  wire [9:0] multiplexer_1_out;

  Multiplexer #(.select(2), .width(10), .enable("false")) multiplexer_1 (
    .in0(Register_Output), .in1(Register_Input), .in2({10{1'b0}}), .in3({10{1'b0}}), .out(multiplexer_1_out),
    .sel({Reset, Write_Enable}));
  _10_bit_Register Register (.Data_Input(multiplexer_1_out), .Clock(Clock), .Data_Output(Register_Output));

  // Notes on the sheet:
  //   reset enable => 10
  //   keep value => 00
  //   write enable => 01
endmodule

module Incrementer (
  input  [9:0] Input,
  output [9:0] Output
);

  wire half_adder_2_carryout, half_adder_3_carryout, half_adder_4_carryout, half_adder_5_carryout,
       half_adder_6_carryout, half_adder_7_carryout, half_adder_8_carryout, half_adder_9_carryout,
       half_adder_10_carryout;

  half_adder half_adder_1 (.B(Input[9]), .A(half_adder_2_carryout), .Sum(Output[9]));  // open: CarryOut
  half_adder half_adder_2 (.B(Input[8]), .A(half_adder_4_carryout), .CarryOut(half_adder_2_carryout), .Sum(Output[8]));
  half_adder half_adder_3 (.B(Input[6]), .A(half_adder_5_carryout), .CarryOut(half_adder_3_carryout), .Sum(Output[6]));
  half_adder half_adder_4 (.B(Input[7]), .A(half_adder_3_carryout), .CarryOut(half_adder_4_carryout), .Sum(Output[7]));
  half_adder half_adder_5 (.B(Input[5]), .A(half_adder_6_carryout), .CarryOut(half_adder_5_carryout), .Sum(Output[5]));
  half_adder half_adder_6 (.B(Input[4]), .A(half_adder_7_carryout), .CarryOut(half_adder_6_carryout), .Sum(Output[4]));
  half_adder half_adder_7 (.B(Input[3]), .A(half_adder_9_carryout), .CarryOut(half_adder_7_carryout), .Sum(Output[3]));
  half_adder half_adder_8 (.B(Input[1]), .A(half_adder_10_carryout), .CarryOut(half_adder_8_carryout), .Sum(Output[1]));
  half_adder half_adder_9 (.B(Input[2]), .A(half_adder_8_carryout), .CarryOut(half_adder_9_carryout), .Sum(Output[2]));
  half_adder half_adder_10 (.B(Input[0]), .A(1'b1), .CarryOut(half_adder_10_carryout), .Sum(Output[0]));
endmodule

module Sign_Extender (
  input  [9:0] _10_bit_Input,
  output [17:0] _18_bit_Input
);

  Multiplexer #(.width(8), .enable("false")) multiplexer_1 (
    .in0({8{1'b0}}), .in1({8{1'b1}}), .out(_18_bit_Input[17:10]), .sel(_10_bit_Input[9]));

  assign _18_bit_Input[9:0] = _10_bit_Input;
endmodule

module Zero_Extender (
  input  [9:0] _10_bit_Input,
  output [17:0] _18_bit_Input
);


  assign _18_bit_Input = {{8{1'b0}}, _10_bit_Input};
endmodule

module Comparator (
  input  A,
  input  B,
  input  in_gt,
  input  in_lt,
  input  in_eq,
  output A_greater_B,
  output A_less_B,
  output A_equal_B
);

  wire and_1_out, and_2_out, not_1_out, xnor_1_out;

  not not_1 (not_1_out, A);
  and and_1 (and_1_out, not_1_out, B, in_eq);
  and and_2 (and_2_out, in_eq, A, ~B);  // AND_Gate
  xnor xnor_1 (xnor_1_out, B, A);
  or or_1 (A_greater_B, in_gt, and_2_out);
  or or_2 (A_less_B, in_lt, and_1_out);
  and and_3 (A_equal_B, in_eq, xnor_1_out);
endmodule

module deneme (
  input  in_1
);


  // Notes on the sheet:
  //   THIS IS FREE AREA, YOU CAN FREELY WORK HERE
endmodule

module Control_Unit (
  input  Start,
  input  [17:0] Instruction,
  input  C_FLAG_IN,
  input  Z_FLAG_IN,
  output RESET_SIG,
  output ADD_SIG,
  output [5:0] Immediate,
  output AND_SIG,
  output [9:0] Address,
  output NAND_SIG,
  output [3:0] Last_4_bits,
  output NOR_SIG,
  output [3:0] Second_4_bits_After_Opcode,
  output [3:0] First_4_bits_After_Opcode,
  output REG_WR,
  output MEM_WR,
  output ALU_IMM,
  output PC_WRT,
  output CMP,
  output LD_SIG,
  output FLG_WR
);

  wire and_1_out, and_2_out, and_3_out, and_4_out, and_5_out, and_6_out, and_7_out, and_8_out, and_9_out,
       and_10_out, and_11_out, and_12_out, and_13_out, and_14_out, and_15_out, and_16_out, and_17_out,
       and_18_out, and_19_out, and_20_out, and_21_out, and_22_out, and_23_out, and_24_out, and_25_out,
       and_26_out, and_31_out, and_32_out, and_33_out, and_34_out, and_35_out, and_36_out, and_37_out,
       clock_1_out, decoder_1_out0, decoder_1_out1, decoder_1_out2, decoder_1_out3, decoder_1_out4,
       decoder_1_out5, decoder_1_out6, decoder_1_out7, decoder_1_out8, decoder_1_out9, decoder_1_out10,
       decoder_1_out11, decoder_1_out12, decoder_1_out13, decoder_1_out14, not_1_out, not_2_out, not_3_out,
       not_4_out, not_5_out, not_6_out, not_7_out, not_8_out, not_9_out, not_10_out, not_11_out, not_12_out,
       not_13_out, not_14_out, not_15_out, not_16_out, not_17_out, not_18_out, not_19_out, not_20_out,
       not_21_out, not_22_out, not_23_out, not_24_out, not_25_out, not_26_out, not_27_out, not_28_out,
       not_29_out, not_30_out, not_31_out, not_32_out, not_33_out, not_34_out, not_35_out, not_36_out,
       not_37_out, not_38_out, not_39_out, not_40_out, not_41_out, not_42_out, not_43_out, not_44_out,
       not_45_out, not_46_out, not_47_out, not_48_out, not_49_out, not_50_out, not_51_out, not_52_out,
       not_53_out, not_54_out, not_55_out, not_56_out, not_57_out, not_58_out, not_59_out, not_61_out,
       not_62_out, not_63_out, not_64_out, not_65_out, not_66_out, not_67_out, NS_Bit0_2, NS_Bit1_2,
       NS_Bit2_2, NS_Bit3_2, or_5_out, or_6_out, or_7_out, or_8_out, or_9_out, or_10_out;
  wire [4:0] n5_bit_reg_file_1_out_4, not_60_out;

  not not_1 (not_1_out, C_FLAG_IN);
  not not_2 (not_2_out, Instruction[15]);
  not not_3 (not_3_out, C_FLAG_IN);
  not not_4 (not_4_out, Instruction[14]);
  not not_5 (not_5_out, Instruction[15]);
  not not_6 (not_6_out, Z_FLAG_IN);
  not not_7 (not_7_out, C_FLAG_IN);
  not not_8 (not_8_out, Instruction[16]);
  not not_9 (not_9_out, Z_FLAG_IN);
  not not_10 (not_10_out, Instruction[14]);
  not not_11 (not_11_out, Instruction[16]);
  not not_12 (not_12_out, Instruction[15]);
  not not_13 (not_13_out, Instruction[16]);
  not not_14 (not_14_out, Instruction[17]);
  not not_15 (not_15_out, C_FLAG_IN);
  not not_16 (not_16_out, Instruction[15]);
  not not_17 (not_17_out, C_FLAG_IN);
  not not_18 (not_18_out, Instruction[14]);
  not not_19 (not_19_out, Instruction[15]);
  not not_20 (not_20_out, Z_FLAG_IN);
  not not_21 (not_21_out, C_FLAG_IN);
  not not_22 (not_22_out, Instruction[16]);
  not not_23 (not_23_out, Z_FLAG_IN);
  not not_24 (not_24_out, Instruction[14]);
  not not_25 (not_25_out, Instruction[16]);
  not not_26 (not_26_out, Instruction[15]);
  not not_27 (not_27_out, Instruction[17]);
  not not_28 (not_28_out, Instruction[16]);
  not not_29 (not_29_out, Instruction[17]);
  and and_1 (and_1_out, not_1_out, Instruction[14], not_2_out, Instruction[16], Instruction[17]);
  and and_2 (and_2_out, Z_FLAG_IN, not_3_out, not_4_out, not_5_out, Instruction[16], Instruction[17]);
  and and_3 (and_3_out, not_6_out, not_7_out, Instruction[14], Instruction[15], not_8_out, Instruction[17]);
  and and_4 (and_4_out, not_9_out, C_FLAG_IN, not_10_out, Instruction[15], not_11_out, Instruction[17]);
  and and_5 (and_5_out, not_12_out, not_13_out, Instruction[17]);
  and and_6 (and_6_out, Instruction[15], Instruction[16], not_14_out);
  and and_7 (and_7_out, not_15_out, Instruction[14], not_16_out, Instruction[16], Instruction[17]);
  and and_8 (and_8_out, Z_FLAG_IN, not_17_out, not_18_out, not_19_out, Instruction[16], Instruction[17]);
  and and_9 (and_9_out, not_20_out, not_21_out, Instruction[14], Instruction[15], not_22_out, Instruction[17]);
  and and_10 (and_10_out, not_23_out, C_FLAG_IN, not_24_out, Instruction[15], not_25_out, Instruction[17]);
  and and_11 (and_11_out, not_26_out, Instruction[16], not_27_out);
  and and_12 (and_12_out, Instruction[15], not_28_out, not_29_out);
  not not_30 (not_30_out, C_FLAG_IN);
  not not_31 (not_31_out, Instruction[15]);
  and and_13 (and_13_out, not_30_out, Instruction[14], not_31_out, Instruction[16], Instruction[17]);
  not not_32 (not_32_out, C_FLAG_IN);
  not not_33 (not_33_out, Instruction[14]);
  and and_14 (and_14_out, Z_FLAG_IN, not_32_out, not_33_out, not_34_out, Instruction[16], Instruction[17]);
  not not_34 (not_34_out, Instruction[15]);
  not not_35 (not_35_out, Instruction[15]);
  and and_15 (and_15_out, not_35_out, not_36_out, Instruction[17]);
  not not_36 (not_36_out, Instruction[16]);
  not not_37 (not_37_out, Instruction[15]);
  and and_16 (and_16_out, not_37_out, Instruction[16], not_38_out);
  not not_38 (not_38_out, Instruction[17]);
  not not_39 (not_39_out, Instruction[15]);
  not not_40 (not_40_out, Instruction[16]);
  and and_17 (and_17_out, not_39_out, not_40_out, not_41_out);
  not not_41 (not_41_out, Instruction[17]);
  not not_42 (not_42_out, Instruction[14]);
  not not_43 (not_43_out, Instruction[14]);
  not not_44 (not_44_out, C_FLAG_IN);
  not not_45 (not_45_out, Instruction[14]);
  not not_46 (not_46_out, Instruction[15]);
  not not_47 (not_47_out, Z_FLAG_IN);
  not not_48 (not_48_out, Instruction[14]);
  not not_49 (not_49_out, Instruction[16]);
  not not_50 (not_50_out, Instruction[14]);
  not not_51 (not_51_out, Instruction[17]);
  not not_52 (not_52_out, Instruction[14]);
  not not_53 (not_53_out, Instruction[15]);
  not not_54 (not_54_out, Instruction[16]);
  or or_1 (NS_Bit3_2, and_1_out, and_2_out, and_3_out, and_4_out, and_5_out, and_6_out);
  and and_18 (and_18_out, Z_FLAG_IN, not_42_out, Instruction[15], Instruction[16], Instruction[17]);
  and and_19 (and_19_out, C_FLAG_IN, not_43_out, Instruction[15], Instruction[16], Instruction[17]);
  and and_20 (and_20_out, Z_FLAG_IN, not_44_out, not_45_out, not_46_out, Instruction[16], Instruction[17]);
  and and_21 (and_21_out, not_47_out, C_FLAG_IN, not_48_out, Instruction[15], not_49_out, Instruction[17]);
  and and_22 (and_22_out, not_50_out, not_51_out);
  and and_23 (and_23_out, not_52_out, not_53_out, not_54_out, Instruction[17]);
  or or_2 (NS_Bit2_2, and_7_out, and_8_out, and_9_out, and_10_out, and_11_out, and_12_out);
  or or_3 (NS_Bit1_2, and_13_out, and_14_out, and_15_out, and_16_out, and_17_out);
  or or_4 (NS_Bit0_2, and_18_out, and_19_out, and_20_out, and_21_out, and_22_out, and_23_out);
  not not_55 (not_55_out, n5_bit_reg_file_1_out_4[1]);
  not not_56 (not_56_out, n5_bit_reg_file_1_out_4[2]);
  and and_24 (and_24_out, n5_bit_reg_file_1_out_4[0], not_55_out, not_56_out, not_57_out, not_58_out);
  not not_57 (not_57_out, n5_bit_reg_file_1_out_4[3]);
  not not_58 (not_58_out, n5_bit_reg_file_1_out_4[4]);
  not not_59 (not_59_out, Instruction[14]);
  and and_25 (and_25_out, not_59_out, Instruction[15], Instruction[16], Instruction[17]);
  and and_26 (and_26_out, NS_Bit0_2, and_24_out);
  and and_27 (not_60_out[1], NS_Bit1_2, and_24_out);
  and and_28 (not_60_out[2], NS_Bit2_2, and_24_out);
  or or_5 (or_5_out, Z_FLAG_IN, C_FLAG_IN);
  Decoder #(.select(4), .enable("false")) decoder_1 (
    .out0(decoder_1_out0), .out1(decoder_1_out1), .out2(decoder_1_out2), .out3(decoder_1_out3),
    .out4(decoder_1_out4), .out5(decoder_1_out5), .out6(decoder_1_out6), .out7(decoder_1_out7),
    .out8(decoder_1_out8), .out9(decoder_1_out9), .out10(decoder_1_out10), .out11(decoder_1_out11),
    .out12(decoder_1_out12), .out13(decoder_1_out13), .out14(decoder_1_out14), .sel(Instruction[17:14]));  // open: out15
  and and_29 (not_60_out[3], NS_Bit3_2, and_24_out);
  and and_30 (not_60_out[4], and_24_out, and_25_out, or_5_out);
  not not_60 (not_60_out[0], and_26_out);
  Clock clock_1 (.out(clock_1_out));
  not not_61 (not_61_out, C_FLAG_IN);
  not not_62 (not_62_out, Z_FLAG_IN);
  _5_bit_Reg_File u_5_bit_reg_file_1 (
    .IN(not_60_out), .Reset(Start), .CLK(clock_1_out), .out_4(n5_bit_reg_file_1_out_4));
  not not_63 (not_63_out, n5_bit_reg_file_1_out_4[1]);
  not not_64 (not_64_out, n5_bit_reg_file_1_out_4[2]);
  not not_65 (not_65_out, n5_bit_reg_file_1_out_4[3]);
  not not_66 (not_66_out, n5_bit_reg_file_1_out_4[4]);
  and and_31 (and_31_out, decoder_1_out10, C_FLAG_IN, not_62_out);
  and and_32 (and_32_out, n5_bit_reg_file_1_out_4[0], not_63_out, not_64_out, not_65_out, not_66_out);
  and and_33 (and_33_out, decoder_1_out11, not_61_out, not_62_out);
  and and_34 (and_34_out, decoder_1_out12, not_61_out, Z_FLAG_IN);
  and and_35 (and_35_out, decoder_1_out13, not_61_out);
  and and_36 (and_36_out, decoder_1_out14, C_FLAG_IN);
  and and_37 (and_37_out, decoder_1_out14, Z_FLAG_IN);
  or or_6 (or_6_out, decoder_1_out0, decoder_1_out4, decoder_1_out9, and_31_out, and_33_out, and_34_out, and_35_out, and_36_out, and_37_out);
  or or_7 (or_7_out, decoder_1_out1, decoder_1_out5);
  or or_8 (or_8_out, decoder_1_out0, decoder_1_out1, decoder_1_out2, decoder_1_out3, decoder_1_out4, decoder_1_out5, decoder_1_out6);
  or or_9 (or_9_out, decoder_1_out4, decoder_1_out5, decoder_1_out9, and_31_out, and_33_out, and_34_out, and_35_out, and_36_out, and_37_out);
  or or_10 (or_10_out, decoder_1_out9, and_31_out, and_33_out, and_34_out, and_35_out, and_36_out, and_37_out);
  not not_67 (not_67_out, n5_bit_reg_file_1_out_4[0]);
  and and_38 (RESET_SIG, not_67_out, not_63_out, not_64_out, not_65_out, not_66_out);
  and and_39 (ADD_SIG, and_32_out, or_6_out);
  and and_40 (AND_SIG, and_32_out, or_7_out);
  and and_41 (NAND_SIG, and_32_out, decoder_1_out2);
  and and_42 (NOR_SIG, and_32_out, decoder_1_out3);
  and and_43 (REG_WR, and_32_out, or_8_out);
  and and_44 (MEM_WR, and_32_out, decoder_1_out7);
  and and_45 (ALU_IMM, and_32_out, or_9_out);
  and and_46 (PC_WRT, and_32_out, or_10_out);
  and and_47 (CMP, and_32_out, decoder_1_out8);
  and and_48 (LD_SIG, and_32_out, decoder_1_out6);
  and and_49 (FLG_WR, and_32_out, decoder_1_out8);

  assign Address = Instruction[9:0];
  assign First_4_bits_After_Opcode = Instruction[13:10];
  assign Immediate = Instruction[5:0];
  assign Last_4_bits = Instruction[3:0];
  assign Second_4_bits_After_Opcode = Instruction[9:6];

  // Other names for the same wires on the sheet: C_Flag = C_FLAG_IN; opcode[3:0] = Instruction[17:14];
  //   Z_Flag = Z_FLAG_IN

  // Notes on the sheet:
  //   state 00001
  //   Z_Flag
  //   C_Flag
  //   Decode Opcode
  //   4
  //   0
  //   Opcode
  //   Send 1, when ALU uses Immediate
endmodule

module Flip_Flop (
  input  D,
  input  Clk,
  output Q
);

  wire d_latch_1_q, not_1_out;

  not not_1 (not_1_out, Clk);
  D_Latch d_latch_1 (.D(D), .Clk(not_1_out), .Q(d_latch_1_q));
  D_Latch d_latch_2 (.D(d_latch_1_q), .Clk(Clk), .Q(Q));
endmodule

module D_Latch (
  input  D,
  input  Clk,
  output Q
);

  wire and_1_out, and_2_out, nor_1_out, not_1_out;

  not not_1 (not_1_out, D);
  and and_1 (and_1_out, D, Clk);
  and and_2 (and_2_out, Clk, not_1_out);
  nor nor_1 (nor_1_out, and_1_out, Q);
  nor nor_2 (Q, nor_1_out, and_2_out);
endmodule

module _18_Bit_Reg (
  input  [17:0] D,
  input  Clk,
  output [17:0] Q
);

  Flip_Flop _0 (.D(D[0]), .Clk(Clk), .Q(Q[0]));
  Flip_Flop _1 (.D(D[1]), .Clk(Clk), .Q(Q[1]));
  Flip_Flop _2 (.D(D[2]), .Clk(Clk), .Q(Q[2]));
  Flip_Flop _3 (.D(D[3]), .Clk(Clk), .Q(Q[3]));
  Flip_Flop _4 (.D(D[4]), .Clk(Clk), .Q(Q[4]));
  Flip_Flop _5 (.D(D[5]), .Clk(Clk), .Q(Q[5]));
  Flip_Flop _6 (.D(D[6]), .Clk(Clk), .Q(Q[6]));
  Flip_Flop _7 (.D(D[7]), .Clk(Clk), .Q(Q[7]));
  Flip_Flop _8 (.D(D[8]), .Clk(Clk), .Q(Q[8]));
  Flip_Flop _9 (.D(D[9]), .Clk(Clk), .Q(Q[9]));
  Flip_Flop _10 (.D(D[10]), .Clk(Clk), .Q(Q[10]));
  Flip_Flop _11 (.D(D[11]), .Clk(Clk), .Q(Q[11]));
  Flip_Flop _12 (.D(D[12]), .Clk(Clk), .Q(Q[12]));
  Flip_Flop _13 (.D(D[13]), .Clk(Clk), .Q(Q[13]));
  Flip_Flop _14 (.D(D[14]), .Clk(Clk), .Q(Q[14]));
  Flip_Flop _15 (.D(D[15]), .Clk(Clk), .Q(Q[15]));
  Flip_Flop _16 (.D(D[16]), .Clk(Clk), .Q(Q[16]));
  Flip_Flop _17 (.D(D[17]), .Clk(Clk), .Q(Q[17]));
endmodule

module Register_File (
  input  Reset,
  input  W_Enabled,
  input  Clock,
  input  [17:0] W_Data,
  input  [3:0] W_Address,
  input  [3:0] R1_Address,
  input  [3:0] R2_Address,
  output [17:0] R1_Data,
  output [17:0] R2_Data
);

  wire decoder_1_out0, decoder_1_out1, decoder_1_out2, decoder_1_out3, decoder_1_out4, decoder_1_out5,
       decoder_1_out6, decoder_1_out7, decoder_1_out8, decoder_1_out9, decoder_1_out10, decoder_1_out11,
       decoder_1_out12, decoder_1_out13, decoder_1_out14, decoder_1_out15, decoder_2_out0, decoder_2_out1,
       decoder_2_out2, decoder_2_out3, decoder_2_out4, decoder_2_out5, decoder_2_out6, decoder_2_out7,
       decoder_2_out8, decoder_2_out9, decoder_2_out10, decoder_2_out11, decoder_2_out12, decoder_2_out13,
       decoder_2_out14, decoder_2_out15, decoder_3_out0, decoder_3_out1, decoder_3_out2, decoder_3_out3,
       decoder_3_out4, decoder_3_out5, decoder_3_out6, decoder_3_out7, decoder_3_out8, decoder_3_out9,
       decoder_3_out10, decoder_3_out11, decoder_3_out12, decoder_3_out13, decoder_3_out14, decoder_3_out15;
  wire [17:0] n18_bit_load_register_1_out_5, n18_bit_load_register_2_out_5, n18_bit_load_register_3_out_5,
       n18_bit_load_register_4_out_5, n18_bit_load_register_5_out_5, n18_bit_load_register_6_out_5,
       n18_bit_load_register_7_out_5, n18_bit_load_register_8_out_5, n18_bit_load_register_9_out_5,
       n18_bit_load_register_10_out_5, n18_bit_load_register_11_out_5, n18_bit_load_register_12_out_5,
       n18_bit_load_register_13_out_5, n18_bit_load_register_14_out_5, n18_bit_load_register_15_out_5,
       n18_bit_load_register_16_out_5;

  Decoder #(.select(4), .disabled(0), .enable("false")) decoder_1 (
    .out0(decoder_1_out0), .out1(decoder_1_out1), .out2(decoder_1_out2), .out3(decoder_1_out3),
    .out4(decoder_1_out4), .out5(decoder_1_out5), .out6(decoder_1_out6), .out7(decoder_1_out7),
    .out8(decoder_1_out8), .out9(decoder_1_out9), .out10(decoder_1_out10), .out11(decoder_1_out11),
    .out12(decoder_1_out12), .out13(decoder_1_out13), .out14(decoder_1_out14), .out15(decoder_1_out15),
    .sel(R1_Address));
  _18_bit_Load_Register u_18_bit_load_register_1 (
    .W_Enable(decoder_2_out0), .Reset(Reset), .out_5(n18_bit_load_register_1_out_5), .Load(W_Data),
    .Clk(Clock));
  _18_bit_Load_Register u_18_bit_load_register_2 (
    .W_Enable(decoder_2_out1), .Reset(Reset), .out_5(n18_bit_load_register_2_out_5), .Load(W_Data),
    .Clk(Clock));
  _18_bit_Load_Register u_18_bit_load_register_3 (
    .W_Enable(decoder_2_out2), .Reset(Reset), .out_5(n18_bit_load_register_3_out_5), .Load(W_Data),
    .Clk(Clock));
  _18_bit_Load_Register u_18_bit_load_register_4 (
    .W_Enable(decoder_2_out3), .Reset(Reset), .out_5(n18_bit_load_register_4_out_5), .Load(W_Data),
    .Clk(Clock));
  _18_bit_Load_Register u_18_bit_load_register_5 (
    .W_Enable(decoder_2_out4), .Reset(Reset), .out_5(n18_bit_load_register_5_out_5), .Load(W_Data),
    .Clk(Clock));
  _18_bit_Load_Register u_18_bit_load_register_6 (
    .W_Enable(decoder_2_out5), .Reset(Reset), .out_5(n18_bit_load_register_6_out_5), .Load(W_Data),
    .Clk(Clock));
  _18_bit_Load_Register u_18_bit_load_register_7 (
    .W_Enable(decoder_2_out6), .Reset(Reset), .out_5(n18_bit_load_register_7_out_5), .Load(W_Data),
    .Clk(Clock));
  _18_bit_Load_Register u_18_bit_load_register_8 (
    .W_Enable(decoder_2_out7), .Reset(Reset), .out_5(n18_bit_load_register_8_out_5), .Load(W_Data),
    .Clk(Clock));
  Decoder #(.select(4), .disabled(0)) decoder_2 (
    .out0(decoder_2_out0), .out1(decoder_2_out1), .out2(decoder_2_out2), .out3(decoder_2_out3),
    .out4(decoder_2_out4), .out5(decoder_2_out5), .out6(decoder_2_out6), .out7(decoder_2_out7),
    .out8(decoder_2_out8), .out9(decoder_2_out9), .out10(decoder_2_out10), .out11(decoder_2_out11),
    .out12(decoder_2_out12), .out13(decoder_2_out13), .out14(decoder_2_out14), .out15(decoder_2_out15),
    .sel(W_Address), .en(W_Enabled));
  assign R1_Data = decoder_1_out0 ? n18_bit_load_register_1_out_5 : 18'bz;  // Controlled_Buffer controlled_buffer_1
  assign R1_Data = decoder_1_out1 ? n18_bit_load_register_2_out_5 : 18'bz;  // Controlled_Buffer controlled_buffer_2
  assign R1_Data = decoder_1_out2 ? n18_bit_load_register_3_out_5 : 18'bz;  // Controlled_Buffer controlled_buffer_3
  assign R1_Data = decoder_1_out3 ? n18_bit_load_register_4_out_5 : 18'bz;  // Controlled_Buffer controlled_buffer_4
  assign R1_Data = decoder_1_out4 ? n18_bit_load_register_5_out_5 : 18'bz;  // Controlled_Buffer controlled_buffer_5
  assign R1_Data = decoder_1_out5 ? n18_bit_load_register_6_out_5 : 18'bz;  // Controlled_Buffer controlled_buffer_6
  assign R1_Data = decoder_1_out6 ? n18_bit_load_register_7_out_5 : 18'bz;  // Controlled_Buffer controlled_buffer_7
  assign R1_Data = decoder_1_out7 ? n18_bit_load_register_8_out_5 : 18'bz;  // Controlled_Buffer controlled_buffer_8
  assign R1_Data = decoder_1_out8 ? n18_bit_load_register_9_out_5 : 18'bz;  // Controlled_Buffer controlled_buffer_9
  assign R1_Data = decoder_1_out9 ? n18_bit_load_register_10_out_5 : 18'bz;  // Controlled_Buffer controlled_buffer_10
  assign R1_Data = decoder_1_out10 ? n18_bit_load_register_11_out_5 : 18'bz;  // Controlled_Buffer controlled_buffer_11
  assign R1_Data = decoder_1_out11 ? n18_bit_load_register_12_out_5 : 18'bz;  // Controlled_Buffer controlled_buffer_12
  assign R1_Data = decoder_1_out12 ? n18_bit_load_register_13_out_5 : 18'bz;  // Controlled_Buffer controlled_buffer_13
  assign R1_Data = decoder_1_out13 ? n18_bit_load_register_14_out_5 : 18'bz;  // Controlled_Buffer controlled_buffer_14
  assign R1_Data = decoder_1_out14 ? n18_bit_load_register_15_out_5 : 18'bz;  // Controlled_Buffer controlled_buffer_15
  _18_bit_Load_Register u_18_bit_load_register_9 (
    .W_Enable(decoder_2_out8), .Reset(Reset), .out_5(n18_bit_load_register_9_out_5), .Load(W_Data),
    .Clk(Clock));
  _18_bit_Load_Register u_18_bit_load_register_10 (
    .W_Enable(decoder_2_out9), .Reset(Reset), .out_5(n18_bit_load_register_10_out_5), .Load(W_Data),
    .Clk(Clock));
  _18_bit_Load_Register u_18_bit_load_register_11 (
    .W_Enable(decoder_2_out10), .Reset(Reset), .out_5(n18_bit_load_register_11_out_5), .Load(W_Data),
    .Clk(Clock));
  _18_bit_Load_Register u_18_bit_load_register_12 (
    .W_Enable(decoder_2_out11), .Reset(Reset), .out_5(n18_bit_load_register_12_out_5), .Load(W_Data),
    .Clk(Clock));
  _18_bit_Load_Register u_18_bit_load_register_13 (
    .W_Enable(decoder_2_out12), .Reset(Reset), .out_5(n18_bit_load_register_13_out_5), .Load(W_Data),
    .Clk(Clock));
  _18_bit_Load_Register u_18_bit_load_register_14 (
    .W_Enable(decoder_2_out13), .Reset(Reset), .out_5(n18_bit_load_register_14_out_5), .Load(W_Data),
    .Clk(Clock));
  _18_bit_Load_Register u_18_bit_load_register_15 (
    .W_Enable(decoder_2_out14), .Reset(Reset), .out_5(n18_bit_load_register_15_out_5), .Load(W_Data),
    .Clk(Clock));
  _18_bit_Load_Register u_18_bit_load_register_16 (
    .W_Enable(decoder_2_out15), .Reset(Reset), .out_5(n18_bit_load_register_16_out_5), .Load(W_Data),
    .Clk(Clock));
  assign R1_Data = decoder_1_out15 ? n18_bit_load_register_16_out_5 : 18'bz;  // Controlled_Buffer controlled_buffer_16
  Decoder #(.select(4), .disabled(0), .enable("false")) decoder_3 (
    .out0(decoder_3_out0), .out1(decoder_3_out1), .out2(decoder_3_out2), .out3(decoder_3_out3),
    .out4(decoder_3_out4), .out5(decoder_3_out5), .out6(decoder_3_out6), .out7(decoder_3_out7),
    .out8(decoder_3_out8), .out9(decoder_3_out9), .out10(decoder_3_out10), .out11(decoder_3_out11),
    .out12(decoder_3_out12), .out13(decoder_3_out13), .out14(decoder_3_out14), .out15(decoder_3_out15),
    .sel(R2_Address));
  assign R2_Data = decoder_3_out0 ? n18_bit_load_register_1_out_5 : 18'bz;  // Controlled_Buffer controlled_buffer_17
  assign R2_Data = decoder_3_out1 ? n18_bit_load_register_2_out_5 : 18'bz;  // Controlled_Buffer controlled_buffer_18
  assign R2_Data = decoder_3_out2 ? n18_bit_load_register_3_out_5 : 18'bz;  // Controlled_Buffer controlled_buffer_19
  assign R2_Data = decoder_3_out3 ? n18_bit_load_register_4_out_5 : 18'bz;  // Controlled_Buffer controlled_buffer_20
  assign R2_Data = decoder_3_out4 ? n18_bit_load_register_5_out_5 : 18'bz;  // Controlled_Buffer controlled_buffer_21
  assign R2_Data = decoder_3_out5 ? n18_bit_load_register_6_out_5 : 18'bz;  // Controlled_Buffer controlled_buffer_22
  assign R2_Data = decoder_3_out6 ? n18_bit_load_register_7_out_5 : 18'bz;  // Controlled_Buffer controlled_buffer_23
  assign R2_Data = decoder_3_out7 ? n18_bit_load_register_8_out_5 : 18'bz;  // Controlled_Buffer controlled_buffer_24
  assign R2_Data = decoder_3_out8 ? n18_bit_load_register_9_out_5 : 18'bz;  // Controlled_Buffer controlled_buffer_25
  assign R2_Data = decoder_3_out9 ? n18_bit_load_register_10_out_5 : 18'bz;  // Controlled_Buffer controlled_buffer_26
  assign R2_Data = decoder_3_out10 ? n18_bit_load_register_11_out_5 : 18'bz;  // Controlled_Buffer controlled_buffer_27
  assign R2_Data = decoder_3_out11 ? n18_bit_load_register_12_out_5 : 18'bz;  // Controlled_Buffer controlled_buffer_28
  assign R2_Data = decoder_3_out12 ? n18_bit_load_register_13_out_5 : 18'bz;  // Controlled_Buffer controlled_buffer_29
  assign R2_Data = decoder_3_out13 ? n18_bit_load_register_14_out_5 : 18'bz;  // Controlled_Buffer controlled_buffer_30
  assign R2_Data = decoder_3_out14 ? n18_bit_load_register_15_out_5 : 18'bz;  // Controlled_Buffer controlled_buffer_31
  assign R2_Data = decoder_3_out15 ? n18_bit_load_register_16_out_5 : 18'bz;  // Controlled_Buffer controlled_buffer_32
endmodule

module _18_bit_Load_Register (
  input  [17:0] Load,
  input  Clk,
  input  W_Enable,
  input  Reset,
  output [17:0] out_5
);

  wire [17:0] multiplexer_1_out;

  Multiplexer #(.select(2), .width(18), .enable("false")) multiplexer_1 (
    .in0(out_5), .in1(Load), .in2({18{1'b0}}), .in3({18{1'b0}}), .out(multiplexer_1_out),
    .sel({Reset, W_Enable}));
  _18_Bit_Reg u_18_bit_reg_1 (.D(multiplexer_1_out), .Clk(Clk), .Q(out_5));
endmodule

module half_adder (
  input  B,
  input  A,
  output CarryOut,
  output Sum
);

  and and_1 (CarryOut, B, A);
  xor xor_1 (Sum, B, A);
endmodule

module full_adder (
  input  B,
  input  A,
  input  Carry_in,
  output CarryOut,
  output Sum
);

  wire and_1_out, and_2_out, and_3_out;

  and and_1 (and_1_out, B, A);
  and and_2 (and_2_out, B, Carry_in);
  or or_1 (CarryOut, and_1_out, and_2_out, and_3_out);
  and and_3 (and_3_out, A, Carry_in);
  ExactlyOne xor_1 (.out(Sum), .in0(B), .in1(A), .in2(Carry_in));
endmodule

// Add
module Adder (
  input  [17:0] B,
  input  [17:0] A,
  output [17:0] Out
);

  wire full_adder_1_carryout, full_adder_2_carryout, full_adder_4_carryout, full_adder_5_carryout,
       full_adder_6_carryout, full_adder_7_carryout, full_adder_8_carryout, full_adder_9_carryout,
       full_adder_10_carryout, full_adder_11_carryout, full_adder_12_carryout, full_adder_13_carryout,
       full_adder_14_carryout, full_adder_15_carryout, full_adder_16_carryout, full_adder_17_carryout,
       half_adder_1_carryout;

  full_adder full_adder_1 (
    .B(B[15]), .A(A[15]), .Carry_in(full_adder_7_carryout), .CarryOut(full_adder_1_carryout), .Sum(Out[15]));
  full_adder full_adder_2 (
    .B(B[16]), .A(A[16]), .Carry_in(full_adder_1_carryout), .CarryOut(full_adder_2_carryout), .Sum(Out[16]));
  full_adder full_adder_3 (.B(B[17]), .A(A[17]), .Carry_in(full_adder_2_carryout), .Sum(Out[17]));  // open: CarryOut
  full_adder full_adder_4 (
    .B(B[11]), .A(A[11]), .Carry_in(full_adder_11_carryout), .CarryOut(full_adder_4_carryout), .Sum(Out[11]));
  full_adder full_adder_5 (
    .B(B[12]), .A(A[12]), .Carry_in(full_adder_4_carryout), .CarryOut(full_adder_5_carryout), .Sum(Out[12]));
  full_adder full_adder_6 (
    .B(B[13]), .A(A[13]), .Carry_in(full_adder_5_carryout), .CarryOut(full_adder_6_carryout), .Sum(Out[13]));
  full_adder full_adder_7 (
    .B(B[14]), .A(A[14]), .Carry_in(full_adder_6_carryout), .CarryOut(full_adder_7_carryout), .Sum(Out[14]));
  full_adder full_adder_8 (
    .B(B[7]), .A(A[7]), .Carry_in(full_adder_15_carryout), .CarryOut(full_adder_8_carryout), .Sum(Out[7]));
  full_adder full_adder_9 (
    .B(B[8]), .A(A[8]), .Carry_in(full_adder_8_carryout), .CarryOut(full_adder_9_carryout), .Sum(Out[8]));
  full_adder full_adder_10 (
    .B(B[9]), .A(A[9]), .Carry_in(full_adder_9_carryout), .CarryOut(full_adder_10_carryout), .Sum(Out[9]));
  full_adder full_adder_11 (
    .B(B[10]), .A(A[10]), .Carry_in(full_adder_10_carryout), .CarryOut(full_adder_11_carryout), .Sum(Out[10]));
  full_adder full_adder_12 (
    .B(B[3]), .A(A[3]), .Carry_in(full_adder_17_carryout), .CarryOut(full_adder_12_carryout), .Sum(Out[3]));
  full_adder full_adder_13 (
    .B(B[4]), .A(A[4]), .Carry_in(full_adder_12_carryout), .CarryOut(full_adder_13_carryout), .Sum(Out[4]));
  full_adder full_adder_14 (
    .B(B[5]), .A(A[5]), .Carry_in(full_adder_13_carryout), .CarryOut(full_adder_14_carryout), .Sum(Out[5]));
  full_adder full_adder_15 (
    .B(B[6]), .A(A[6]), .Carry_in(full_adder_14_carryout), .CarryOut(full_adder_15_carryout), .Sum(Out[6]));
  half_adder half_adder_1 (.B(B[0]), .A(A[0]), .CarryOut(half_adder_1_carryout), .Sum(Out[0]));
  full_adder full_adder_16 (
    .B(B[1]), .A(A[1]), .Carry_in(half_adder_1_carryout), .CarryOut(full_adder_16_carryout), .Sum(Out[1]));
  full_adder full_adder_17 (
    .B(B[2]), .A(A[2]), .Carry_in(full_adder_16_carryout), .CarryOut(full_adder_17_carryout), .Sum(Out[2]));
endmodule

module And (
  input  [17:0] A,
  input  [17:0] B,
  output [17:0] Out
);

  assign Out = A & B;  // AND_Gate and_1, 18 bits wide
endmodule

module Nand (
  input  [17:0] A,
  input  [17:0] B,
  output [17:0] Out
);

  wire [17:0] and_1_out;

  assign and_1_out = A & B;  // AND_Gate and_1, 18 bits wide
  assign Out = ~and_1_out;  // NOT_Gate not_1, 18 bits wide
endmodule

module Nor (
  input  [17:0] A,
  input  [17:0] B,
  output [17:0] Out
);

  wire [17:0] or_1_out;

  assign or_1_out = A | B;  // OR_Gate or_1, 18 bits wide
  assign Out = ~or_1_out;  // NOT_Gate not_1, 18 bits wide
endmodule

module ALU (
  input  [17:0] A,
  input  [17:0] B,
  input  ADD,
  input  AND,
  input  NAND,
  input  NOR,
  output [17:0] Out
);

  wire [17:0] adder_1_out, and_1_out, nand_1_out, nor_1_out;

  And and_1 (.A(A), .B(B), .Out(and_1_out));
  Adder adder_1 (.B(B), .A(A), .Out(adder_1_out));
  assign Out = ADD ? adder_1_out : 18'bz;  // Controlled_Buffer controlled_buffer_1
  assign Out = AND ? and_1_out : 18'bz;  // Controlled_Buffer controlled_buffer_2
  Nor nor_1 (.A(A), .B(B), .Out(nor_1_out));
  Nand nand_1 (.A(A), .B(B), .Out(nand_1_out));
  assign Out = NAND ? nand_1_out : 18'bz;  // Controlled_Buffer controlled_buffer_3
  assign Out = NOR ? nor_1_out : 18'bz;  // Controlled_Buffer controlled_buffer_4
endmodule

module \_1bıt_magnitude_comparator  (
  input  a,
  input  i_gt,
  input  i_eq,
  input  i_lt,
  input  b,
  output o_gt,
  output o_eq,
  output o_lt
);

  wire and_1_out, and_2_out, not_1_out, not_2_out, xnor_1_out;

  not not_1 (not_1_out, b);
  not not_2 (not_2_out, a);
  and and_1 (and_1_out, a, i_eq, not_1_out);
  xnor xnor_1 (xnor_1_out, a, b);
  and and_2 (and_2_out, not_2_out, i_eq, b);
  or or_1 (o_gt, i_gt, and_1_out);
  and and_3 (o_eq, i_eq, xnor_1_out);
  or or_2 (o_lt, i_lt, and_2_out);
endmodule

module _18bit_magnitude_comparator (
  input  [17:0] a,
  input  [17:0] b,
  output O_GRT,
  output O_EQL,
  output O_LT
);

  wire \n1bıt_magnitude_comparator_1_o_eq , \n1bıt_magnitude_comparator_1_o_gt ,
       \n1bıt_magnitude_comparator_1_o_lt , \n1bıt_magnitude_comparator_2_o_eq ,
       \n1bıt_magnitude_comparator_2_o_gt , \n1bıt_magnitude_comparator_2_o_lt ,
       \n1bıt_magnitude_comparator_3_o_eq , \n1bıt_magnitude_comparator_3_o_gt ,
       \n1bıt_magnitude_comparator_3_o_lt , \n1bıt_magnitude_comparator_4_o_eq ,
       \n1bıt_magnitude_comparator_4_o_gt , \n1bıt_magnitude_comparator_4_o_lt ,
       \n1bıt_magnitude_comparator_5_o_eq , \n1bıt_magnitude_comparator_5_o_gt ,
       \n1bıt_magnitude_comparator_5_o_lt , \n1bıt_magnitude_comparator_6_o_eq ,
       \n1bıt_magnitude_comparator_6_o_gt , \n1bıt_magnitude_comparator_6_o_lt ,
       \n1bıt_magnitude_comparator_7_o_eq , \n1bıt_magnitude_comparator_7_o_gt ,
       \n1bıt_magnitude_comparator_7_o_lt , \n1bıt_magnitude_comparator_8_o_eq ,
       \n1bıt_magnitude_comparator_8_o_gt , \n1bıt_magnitude_comparator_8_o_lt ,
       \n1bıt_magnitude_comparator_9_o_eq , \n1bıt_magnitude_comparator_9_o_gt ,
       \n1bıt_magnitude_comparator_9_o_lt , \n1bıt_magnitude_comparator_10_o_eq ,
       \n1bıt_magnitude_comparator_10_o_gt , \n1bıt_magnitude_comparator_10_o_lt ,
       \n1bıt_magnitude_comparator_11_o_eq , \n1bıt_magnitude_comparator_11_o_gt ,
       \n1bıt_magnitude_comparator_11_o_lt , \n1bıt_magnitude_comparator_12_o_eq ,
       \n1bıt_magnitude_comparator_12_o_gt , \n1bıt_magnitude_comparator_12_o_lt ,
       \n1bıt_magnitude_comparator_13_o_eq , \n1bıt_magnitude_comparator_13_o_gt ,
       \n1bıt_magnitude_comparator_13_o_lt , \n1bıt_magnitude_comparator_14_o_eq ,
       \n1bıt_magnitude_comparator_14_o_gt , \n1bıt_magnitude_comparator_14_o_lt ,
       \n1bıt_magnitude_comparator_15_o_eq , \n1bıt_magnitude_comparator_15_o_gt ,
       \n1bıt_magnitude_comparator_15_o_lt , \n1bıt_magnitude_comparator_16_o_eq ,
       \n1bıt_magnitude_comparator_16_o_gt , \n1bıt_magnitude_comparator_16_o_lt ,
       \n1bıt_magnitude_comparator_17_o_eq , \n1bıt_magnitude_comparator_17_o_gt ,
       \n1bıt_magnitude_comparator_17_o_lt ;

  \_1bıt_magnitude_comparator  \u_1bıt_magnitude_comparator_1  (
    .i_gt(1'b0), .i_eq(1'b1), .i_lt(1'b0), .a(a[17]), .b(b[17]), .o_gt(\n1bıt_magnitude_comparator_1_o_gt ),
    .o_eq(\n1bıt_magnitude_comparator_1_o_eq ), .o_lt(\n1bıt_magnitude_comparator_1_o_lt ));
  \_1bıt_magnitude_comparator  \u_1bıt_magnitude_comparator_2  (
    .i_gt(\n1bıt_magnitude_comparator_1_o_gt ), .i_eq(\n1bıt_magnitude_comparator_1_o_eq ),
    .i_lt(\n1bıt_magnitude_comparator_1_o_lt ), .a(a[16]), .b(b[16]),
    .o_gt(\n1bıt_magnitude_comparator_2_o_gt ), .o_eq(\n1bıt_magnitude_comparator_2_o_eq ),
    .o_lt(\n1bıt_magnitude_comparator_2_o_lt ));
  \_1bıt_magnitude_comparator  \u_1bıt_magnitude_comparator_3  (
    .i_gt(\n1bıt_magnitude_comparator_2_o_gt ), .i_eq(\n1bıt_magnitude_comparator_2_o_eq ),
    .i_lt(\n1bıt_magnitude_comparator_2_o_lt ), .a(a[15]), .b(b[15]),
    .o_gt(\n1bıt_magnitude_comparator_3_o_gt ), .o_eq(\n1bıt_magnitude_comparator_3_o_eq ),
    .o_lt(\n1bıt_magnitude_comparator_3_o_lt ));
  \_1bıt_magnitude_comparator  \u_1bıt_magnitude_comparator_4  (
    .i_gt(\n1bıt_magnitude_comparator_3_o_gt ), .i_eq(\n1bıt_magnitude_comparator_3_o_eq ),
    .i_lt(\n1bıt_magnitude_comparator_3_o_lt ), .a(a[14]), .b(b[14]),
    .o_gt(\n1bıt_magnitude_comparator_4_o_gt ), .o_eq(\n1bıt_magnitude_comparator_4_o_eq ),
    .o_lt(\n1bıt_magnitude_comparator_4_o_lt ));
  \_1bıt_magnitude_comparator  \u_1bıt_magnitude_comparator_5  (
    .i_gt(\n1bıt_magnitude_comparator_4_o_gt ), .i_eq(\n1bıt_magnitude_comparator_4_o_eq ),
    .i_lt(\n1bıt_magnitude_comparator_4_o_lt ), .a(a[13]), .b(b[13]),
    .o_gt(\n1bıt_magnitude_comparator_5_o_gt ), .o_eq(\n1bıt_magnitude_comparator_5_o_eq ),
    .o_lt(\n1bıt_magnitude_comparator_5_o_lt ));
  \_1bıt_magnitude_comparator  \u_1bıt_magnitude_comparator_6  (
    .i_gt(\n1bıt_magnitude_comparator_5_o_gt ), .i_eq(\n1bıt_magnitude_comparator_5_o_eq ),
    .i_lt(\n1bıt_magnitude_comparator_5_o_lt ), .a(a[12]), .b(b[12]),
    .o_gt(\n1bıt_magnitude_comparator_6_o_gt ), .o_eq(\n1bıt_magnitude_comparator_6_o_eq ),
    .o_lt(\n1bıt_magnitude_comparator_6_o_lt ));
  \_1bıt_magnitude_comparator  \u_1bıt_magnitude_comparator_7  (
    .i_gt(\n1bıt_magnitude_comparator_6_o_gt ), .i_eq(\n1bıt_magnitude_comparator_6_o_eq ),
    .i_lt(\n1bıt_magnitude_comparator_6_o_lt ), .a(a[11]), .b(b[11]),
    .o_gt(\n1bıt_magnitude_comparator_7_o_gt ), .o_eq(\n1bıt_magnitude_comparator_7_o_eq ),
    .o_lt(\n1bıt_magnitude_comparator_7_o_lt ));
  \_1bıt_magnitude_comparator  \u_1bıt_magnitude_comparator_8  (
    .i_gt(\n1bıt_magnitude_comparator_7_o_gt ), .i_eq(\n1bıt_magnitude_comparator_7_o_eq ),
    .i_lt(\n1bıt_magnitude_comparator_7_o_lt ), .a(a[10]), .b(b[10]),
    .o_gt(\n1bıt_magnitude_comparator_8_o_gt ), .o_eq(\n1bıt_magnitude_comparator_8_o_eq ),
    .o_lt(\n1bıt_magnitude_comparator_8_o_lt ));
  \_1bıt_magnitude_comparator  \u_1bıt_magnitude_comparator_9  (
    .i_gt(\n1bıt_magnitude_comparator_8_o_gt ), .i_eq(\n1bıt_magnitude_comparator_8_o_eq ),
    .i_lt(\n1bıt_magnitude_comparator_8_o_lt ), .a(a[9]), .b(b[9]),
    .o_gt(\n1bıt_magnitude_comparator_9_o_gt ), .o_eq(\n1bıt_magnitude_comparator_9_o_eq ),
    .o_lt(\n1bıt_magnitude_comparator_9_o_lt ));
  \_1bıt_magnitude_comparator  \u_1bıt_magnitude_comparator_10  (
    .i_gt(\n1bıt_magnitude_comparator_11_o_gt ), .i_eq(\n1bıt_magnitude_comparator_11_o_eq ),
    .i_lt(\n1bıt_magnitude_comparator_11_o_lt ), .a(a[7]), .b(b[7]),
    .o_gt(\n1bıt_magnitude_comparator_10_o_gt ), .o_eq(\n1bıt_magnitude_comparator_10_o_eq ),
    .o_lt(\n1bıt_magnitude_comparator_10_o_lt ));
  \_1bıt_magnitude_comparator  \u_1bıt_magnitude_comparator_11  (
    .i_gt(\n1bıt_magnitude_comparator_9_o_gt ), .i_eq(\n1bıt_magnitude_comparator_9_o_eq ),
    .i_lt(\n1bıt_magnitude_comparator_9_o_lt ), .a(a[8]), .b(b[8]),
    .o_gt(\n1bıt_magnitude_comparator_11_o_gt ), .o_eq(\n1bıt_magnitude_comparator_11_o_eq ),
    .o_lt(\n1bıt_magnitude_comparator_11_o_lt ));
  \_1bıt_magnitude_comparator  \u_1bıt_magnitude_comparator_12  (
    .i_gt(\n1bıt_magnitude_comparator_10_o_gt ), .i_eq(\n1bıt_magnitude_comparator_10_o_eq ),
    .i_lt(\n1bıt_magnitude_comparator_10_o_lt ), .a(a[6]), .b(b[6]),
    .o_gt(\n1bıt_magnitude_comparator_12_o_gt ), .o_eq(\n1bıt_magnitude_comparator_12_o_eq ),
    .o_lt(\n1bıt_magnitude_comparator_12_o_lt ));
  \_1bıt_magnitude_comparator  \u_1bıt_magnitude_comparator_13  (
    .i_gt(\n1bıt_magnitude_comparator_12_o_gt ), .i_eq(\n1bıt_magnitude_comparator_12_o_eq ),
    .i_lt(\n1bıt_magnitude_comparator_12_o_lt ), .a(a[5]), .b(b[5]),
    .o_gt(\n1bıt_magnitude_comparator_13_o_gt ), .o_eq(\n1bıt_magnitude_comparator_13_o_eq ),
    .o_lt(\n1bıt_magnitude_comparator_13_o_lt ));
  \_1bıt_magnitude_comparator  \u_1bıt_magnitude_comparator_14  (
    .i_gt(\n1bıt_magnitude_comparator_13_o_gt ), .i_eq(\n1bıt_magnitude_comparator_13_o_eq ),
    .i_lt(\n1bıt_magnitude_comparator_13_o_lt ), .a(a[4]), .b(b[4]),
    .o_gt(\n1bıt_magnitude_comparator_14_o_gt ), .o_eq(\n1bıt_magnitude_comparator_14_o_eq ),
    .o_lt(\n1bıt_magnitude_comparator_14_o_lt ));
  \_1bıt_magnitude_comparator  \u_1bıt_magnitude_comparator_15  (
    .i_gt(\n1bıt_magnitude_comparator_14_o_gt ), .i_eq(\n1bıt_magnitude_comparator_14_o_eq ),
    .i_lt(\n1bıt_magnitude_comparator_14_o_lt ), .a(a[3]), .b(b[3]),
    .o_gt(\n1bıt_magnitude_comparator_15_o_gt ), .o_eq(\n1bıt_magnitude_comparator_15_o_eq ),
    .o_lt(\n1bıt_magnitude_comparator_15_o_lt ));
  \_1bıt_magnitude_comparator  \u_1bıt_magnitude_comparator_16  (
    .i_gt(\n1bıt_magnitude_comparator_15_o_gt ), .i_eq(\n1bıt_magnitude_comparator_15_o_eq ),
    .i_lt(\n1bıt_magnitude_comparator_15_o_lt ), .a(a[2]), .b(b[2]),
    .o_gt(\n1bıt_magnitude_comparator_16_o_gt ), .o_eq(\n1bıt_magnitude_comparator_16_o_eq ),
    .o_lt(\n1bıt_magnitude_comparator_16_o_lt ));
  \_1bıt_magnitude_comparator  \u_1bıt_magnitude_comparator_17  (
    .i_gt(\n1bıt_magnitude_comparator_16_o_gt ), .i_eq(\n1bıt_magnitude_comparator_16_o_eq ),
    .i_lt(\n1bıt_magnitude_comparator_16_o_lt ), .a(a[1]), .b(b[1]),
    .o_gt(\n1bıt_magnitude_comparator_17_o_gt ), .o_eq(\n1bıt_magnitude_comparator_17_o_eq ),
    .o_lt(\n1bıt_magnitude_comparator_17_o_lt ));
  \_1bıt_magnitude_comparator  \u_1bıt_magnitude_comparator_18  (
    .i_gt(\n1bıt_magnitude_comparator_17_o_gt ), .i_eq(\n1bıt_magnitude_comparator_17_o_eq ),
    .i_lt(\n1bıt_magnitude_comparator_17_o_lt ), .a(a[0]), .b(b[0]), .o_gt(O_GRT), .o_eq(O_EQL), .o_lt(O_LT));
endmodule

module main_Yusuf (
  output [9:0] PC_Output,
  output [17:0] INSTRUCTION
);

  wire clock_1_out, CMP_o_eql, CMP_o_lt, control_unit_1_add_sig, control_unit_1_alu_imm,
       control_unit_1_and_sig, control_unit_1_cmp, control_unit_1_mem_wr, control_unit_1_nand_sig,
       control_unit_1_nor_sig, control_unit_1_pc_wrt, control_unit_1_reg_wr, flag_file_1_c_out,
       flag_file_1_z_out, not_1_out, not_2_out, undriven;
  wire [3:0] control_unit_1_first_4_bits_after_opcode, control_unit_1_last_4_bits,
       control_unit_1_second_4_bits_after_opcode, multiplexer_3_out;
  wire [5:0] control_unit_1_immediate;
  wire [9:0] control_unit_1_address, multiplexer_1_out;
  wire [17:0] alu_1_out, multiplexer_2_out, multiplexer_4_out, multiplexer_5_out,
       n6_bit_sign_extender_1__18_bit_input, register_file_1_r1_data, register_file_1_r2_data,
       sign_extender_1__18_bit_input, sign_extender_2__18_bit_input;

  Clock clock_1 (.out(clock_1_out));
  not not_1 (not_1_out, control_unit_1_pc_wrt);
  Flag_File flag_file_1 (
    .Write_Enable(control_unit_1_cmp), .Reset(undriven), .Clk(clock_1_out), .C_IN(CMP_o_lt),
    .Z_IN(CMP_o_eql), .C_OUT(flag_file_1_c_out), .Z_OUT(flag_file_1_z_out));
  Control_Unit control_unit_1 (
    .Instruction(INSTRUCTION), .First_4_bits_After_Opcode(control_unit_1_first_4_bits_after_opcode),
    .Last_4_bits(control_unit_1_last_4_bits),
    .Second_4_bits_After_Opcode(control_unit_1_second_4_bits_after_opcode), .Address(control_unit_1_address),
    .Immediate(control_unit_1_immediate), .ADD_SIG(control_unit_1_add_sig), .REG_WR(control_unit_1_reg_wr),
    .MEM_WR(control_unit_1_mem_wr), .ALU_IMM(control_unit_1_alu_imm), .CMP(control_unit_1_cmp),
    .Z_FLAG_IN(flag_file_1_z_out), .C_FLAG_IN(flag_file_1_c_out), .PC_WRT(control_unit_1_pc_wrt),
    .NOR_SIG(control_unit_1_nor_sig), .AND_SIG(control_unit_1_and_sig), .NAND_SIG(control_unit_1_nand_sig),
    .Start(clock_1_out));  // open: LD_SIG, FLG_WR, RESET_SIG
  Program_Counter program_counter_1 (
    .Input(alu_1_out[9:0]), .Increment(not_1_out), .Write_Address(control_unit_1_pc_wrt), .Output(PC_Output),
    .Reset(undriven), .Clock(clock_1_out));
  _6_bit_Sign_Extender u_6_bit_sign_extender_1 (
    .in_1(control_unit_1_immediate), ._18_bit_Input(n6_bit_sign_extender_1__18_bit_input));
  Multiplexer #(.width(10), .enable("false")) multiplexer_1 (
    .in0(PC_Output), .in1(control_unit_1_address), .out(multiplexer_1_out));  // open: sel
  Sign_Extender sign_extender_1 (._10_bit_Input(control_unit_1_address), ._18_bit_Input(sign_extender_1__18_bit_input));
  not not_2 (not_2_out, control_unit_1_mem_wr);
  RAM #(.addrWidth(10), .dataWidth(18)) ram_1 (
    .addr(multiplexer_1_out), .data(INSTRUCTION), .sel(1'b1), .ld(not_2_out));  // open: clk, clr
  Register_File register_file_1 (
    .W_Data(alu_1_out), .W_Address(control_unit_1_first_4_bits_after_opcode), .Reset(undriven),
    .R1_Data(register_file_1_r1_data), .Clock(clock_1_out), .W_Enabled(control_unit_1_reg_wr),
    .R2_Data(register_file_1_r2_data), .R2_Address(multiplexer_3_out), .R1_Address(control_unit_1_last_4_bits));
  Sign_Extender sign_extender_2 (._10_bit_Input(PC_Output), ._18_bit_Input(sign_extender_2__18_bit_input));
  _18bit_magnitude_comparator CMP (
    .a(register_file_1_r2_data), .b(register_file_1_r1_data), .O_EQL(CMP_o_eql), .O_LT(CMP_o_lt));  // open: O_GRT
  Multiplexer #(.width(18), .enable("false")) multiplexer_2 (
    .in0(register_file_1_r1_data), .in1(sign_extender_2__18_bit_input), .out(multiplexer_2_out),
    .sel(control_unit_1_pc_wrt));
  Multiplexer #(.width(4), .enable("false")) multiplexer_3 (
    .in0(control_unit_1_first_4_bits_after_opcode), .in1(control_unit_1_second_4_bits_after_opcode),
    .out(multiplexer_3_out), .sel(control_unit_1_mem_wr));
  Multiplexer #(.width(18), .enable("false")) multiplexer_4 (
    .in0(n6_bit_sign_extender_1__18_bit_input), .in1(sign_extender_1__18_bit_input), .out(multiplexer_4_out),
    .sel(control_unit_1_pc_wrt));
  Multiplexer #(.width(18), .enable("false")) multiplexer_5 (
    .in0(register_file_1_r2_data), .in1(multiplexer_4_out), .out(multiplexer_5_out),
    .sel(control_unit_1_alu_imm));
  ALU alu_1 (
    .ADD(control_unit_1_add_sig), .AND(control_unit_1_and_sig), .NAND(control_unit_1_nand_sig),
    .NOR(control_unit_1_nor_sig), .A(multiplexer_2_out), .B(multiplexer_5_out), .Out(alu_1_out));

  // Notes on the sheet:
  //   RAM
  //   Careful: To get the first 4 bits of instuction, you have to get bits: 17,16,15,14
  //   2nd or 1st after opcode
  //   imm or addr
endmodule

module Flag_File (
  input  C_IN,
  input  Z_IN,
  input  Write_Enable,
  input  Reset,
  input  Clk,
  output C_OUT,
  output Z_OUT
);

  Load_Flag_Register Carry_Flag (.Write_Enable(Write_Enable), .Reset(Reset), .Clk(Clk), .D(C_IN), .Q(C_OUT));
  Load_Flag_Register Zero_Flag (.Write_Enable(Write_Enable), .Reset(Reset), .Clk(Clk), .D(Z_IN), .Q(Z_OUT));
endmodule

module Load_Flag_Register (
  input  D,
  input  Write_Enable,
  input  Reset,
  input  Clk,
  output Q
);

  wire multiplexer_1_out;

  Multiplexer #(.select(2), .enable("false")) multiplexer_1 (
    .in0(Q), .in1(D), .in2(1'b0), .in3(1'b0), .out(multiplexer_1_out), .sel({Reset, Write_Enable}));
  Flip_Flop Carry_Flag (.D(multiplexer_1_out), .Clk(Clk), .Q(Q));
endmodule

module _6_bit_Sign_Extender (
  input  [5:0] in_1,
  output [17:0] _18_bit_Input
);

  Multiplexer #(.width(12), .enable("false")) multiplexer_1 (
    .in0({12{1'b0}}), .in1({12{1'b1}}), .out(_18_bit_Input[17:6]), .sel(in_1[5]));

  assign _18_bit_Input[5:0] = in_1;
endmodule

module _5_bit_Reg (
  input  [4:0] in_1,
  input  CLK,
  output [4:0] out_3
);

  Flip_Flop ff_1 (.D(in_1[0]), .Clk(CLK), .Q(out_3[0]));
  Flip_Flop ff_2 (.D(in_1[1]), .Clk(CLK), .Q(out_3[1]));
  Flip_Flop ff_3 (.D(in_1[2]), .Clk(CLK), .Q(out_3[2]));
  Flip_Flop ff_4 (.D(in_1[3]), .Clk(CLK), .Q(out_3[3]));
  Flip_Flop ff_5 (.D(in_1[4]), .Clk(CLK), .Q(out_3[4]));
endmodule

module _5_bit_Reg_File (
  input  [4:0] IN,
  input  Reset,
  input  CLK,
  output [4:0] out_4
);

  wire [4:0] multiplexer_1_out;

  Multiplexer #(.width(5), .enable("false")) multiplexer_1 (
    .in0(IN), .in1({5{1'b0}}), .out(multiplexer_1_out), .sel(Reset));
  _5_bit_Reg u_5_bit_reg_1 (.in_1(multiplexer_1_out), .CLK(CLK), .out_3(out_4));
endmodule
