// Logisim project logism-design.circ as structural Verilog
module D_Latch (
  input  D,
  input  Clk,
  output Q
);

  wire and_1_out, and_2_out, nor_1_out, not_1_out;

  not not_1 (not_1_out, D);
  and and_1 (and_1_out, D, Clk);
  and and_2 (and_2_out, Clk, not_1_out);
  nor nor_1 (nor_1_out, and_1_out, Q);
  nor nor_2 (Q, nor_1_out, and_2_out);
endmodule

module Flip_Flop (
  input  D,
  input  Clk,
  output Q
);

  wire d_latch_1_q, not_1_out;

  not not_1 (not_1_out, Clk);
  D_Latch d_latch_1 (.D(D), .Clk(not_1_out), .Q(d_latch_1_q));
  D_Latch d_latch_2 (.D(d_latch_1_q), .Clk(Clk), .Q(Q));
endmodule

module _18_Bit_Reg (
  input  [17:0] D,
  input  Clk,
  output [17:0] Q
);

  Flip_Flop _0 (.D(D[0]), .Clk(Clk), .Q(Q[0]));
  Flip_Flop _1 (.D(D[1]), .Clk(Clk), .Q(Q[1]));
  Flip_Flop _2 (.D(D[2]), .Clk(Clk), .Q(Q[2]));
  Flip_Flop _3 (.D(D[3]), .Clk(Clk), .Q(Q[3]));
  Flip_Flop _4 (.D(D[4]), .Clk(Clk), .Q(Q[4]));
  Flip_Flop _5 (.D(D[5]), .Clk(Clk), .Q(Q[5]));
  Flip_Flop _6 (.D(D[6]), .Clk(Clk), .Q(Q[6]));
  Flip_Flop _7 (.D(D[7]), .Clk(Clk), .Q(Q[7]));
  Flip_Flop _8 (.D(D[8]), .Clk(Clk), .Q(Q[8]));
  Flip_Flop _9 (.D(Clk), .Clk(Clk), .Q(Q[9]));
  Flip_Flop _10 (.D(Clk), .Clk(Clk), .Q(Q[10]));
  Flip_Flop _11 (.D(D[11]), .Clk(Clk), .Q(Q[11]));
  Flip_Flop _12 (.D(D[12]), .Clk(Clk), .Q(Q[12]));
  Flip_Flop _13 (.D(D[13]), .Clk(Clk), .Q(Q[13]));
  Flip_Flop _14 (.D(D[14]), .Clk(Clk), .Q(Q[14]));
  Flip_Flop _15 (.D(D[15]), .Clk(Clk), .Q(Q[15]));
  Flip_Flop _16 (.D(D[16]), .Clk(Clk), .Q(Q[16]));
  Flip_Flop _17 (.D(D[17]), .Clk(Clk), .Q(Q[17]));

  assign D[10:9] = {2{Clk}};
endmodule

module Register_File (
);

  _18_Bit_Reg u_18_bit_reg_1 ();  // open: D, Clk, Q
endmodule
