// Logisim project ALU.circ as structural Verilog
module half_adder (
  input  B,
  input  A,
  output CarryOut,
  output Sum
);

  and and_1 (CarryOut, B, A);
  xor xor_1 (Sum, B, A);
endmodule

module full_adder (
  input  B,
  input  A,
  input  Carry_in,
  output CarryOut,
  output Sum
);

  wire and_1_out, and_2_out, and_3_out;

  and and_1 (and_1_out, B, A);
  and and_2 (and_2_out, B, Carry_in);
  or or_1 (CarryOut, and_1_out, and_2_out, and_3_out);
  and and_3 (and_3_out, A, Carry_in);
  ExactlyOne xor_1 (.out(Sum), .in0(B), .in1(A), .in2(Carry_in));
endmodule

// Add
module Adder (
  input  [17:0] B,
  input  [17:0] A,
  output [17:0] Out
);

  wire full_adder_1_carryout, full_adder_2_carryout, full_adder_4_carryout, full_adder_5_carryout,
       full_adder_6_carryout, full_adder_7_carryout, full_adder_8_carryout, full_adder_9_carryout,
       full_adder_10_carryout, full_adder_11_carryout, full_adder_12_carryout, full_adder_13_carryout,
       full_adder_14_carryout, full_adder_15_carryout, full_adder_16_carryout, full_adder_17_carryout,
       half_adder_1_carryout;

  full_adder full_adder_1 (
    .B(B[15]), .A(A[15]), .Carry_in(full_adder_7_carryout), .CarryOut(full_adder_1_carryout), .Sum(Out[15]));
  full_adder full_adder_2 (
    .B(B[16]), .A(A[16]), .Carry_in(full_adder_1_carryout), .CarryOut(full_adder_2_carryout), .Sum(Out[16]));
  full_adder full_adder_3 (.B(B[17]), .A(A[17]), .Carry_in(full_adder_2_carryout), .Sum(Out[17]));  // open: CarryOut
  full_adder full_adder_4 (
    .B(B[11]), .A(A[11]), .Carry_in(full_adder_11_carryout), .CarryOut(full_adder_4_carryout), .Sum(Out[11]));
  full_adder full_adder_5 (
    .B(B[12]), .A(A[12]), .Carry_in(full_adder_4_carryout), .CarryOut(full_adder_5_carryout), .Sum(Out[12]));
  full_adder full_adder_6 (
    .B(B[13]), .A(A[13]), .Carry_in(full_adder_5_carryout), .CarryOut(full_adder_6_carryout), .Sum(Out[13]));
  full_adder full_adder_7 (
    .B(B[14]), .A(A[14]), .Carry_in(full_adder_6_carryout), .CarryOut(full_adder_7_carryout), .Sum(Out[14]));
  full_adder full_adder_8 (
    .B(B[7]), .A(A[7]), .Carry_in(full_adder_15_carryout), .CarryOut(full_adder_8_carryout), .Sum(Out[7]));
  full_adder full_adder_9 (
    .B(B[8]), .A(A[8]), .Carry_in(full_adder_8_carryout), .CarryOut(full_adder_9_carryout), .Sum(Out[8]));
  full_adder full_adder_10 (
    .B(B[9]), .A(A[9]), .Carry_in(full_adder_9_carryout), .CarryOut(full_adder_10_carryout), .Sum(Out[9]));
  full_adder full_adder_11 (
    .B(B[10]), .A(A[10]), .Carry_in(full_adder_10_carryout), .CarryOut(full_adder_11_carryout), .Sum(Out[10]));
  full_adder full_adder_12 (
    .B(B[3]), .A(A[3]), .Carry_in(full_adder_17_carryout), .CarryOut(full_adder_12_carryout), .Sum(Out[3]));
  full_adder full_adder_13 (
    .B(B[4]), .A(A[4]), .Carry_in(full_adder_12_carryout), .CarryOut(full_adder_13_carryout), .Sum(Out[4]));
  full_adder full_adder_14 (
    .B(B[5]), .A(A[5]), .Carry_in(full_adder_13_carryout), .CarryOut(full_adder_14_carryout), .Sum(Out[5]));
  full_adder full_adder_15 (
    .B(B[6]), .A(A[6]), .Carry_in(full_adder_14_carryout), .CarryOut(full_adder_15_carryout), .Sum(Out[6]));
  half_adder half_adder_1 (.B(B[0]), .A(A[0]), .CarryOut(half_adder_1_carryout), .Sum(Out[0]));
  full_adder full_adder_16 (
    .B(B[1]), .A(A[1]), .Carry_in(half_adder_1_carryout), .CarryOut(full_adder_16_carryout), .Sum(Out[1]));
  full_adder full_adder_17 (
    .B(B[2]), .A(A[2]), .Carry_in(full_adder_16_carryout), .CarryOut(full_adder_17_carryout), .Sum(Out[2]));
endmodule

module And (
  input  [17:0] A,
  input  [17:0] B,
  output [17:0] Out
);

  assign Out = A & B;  // AND_Gate and_1, 18 bits wide
endmodule

module Nand (
  input  [17:0] A,
  input  [17:0] B,
  output [17:0] Out
);

  wire [17:0] and_1_out;

  assign and_1_out = A & B;  // AND_Gate and_1, 18 bits wide
  assign Out = ~and_1_out;  // NOT_Gate not_1, 18 bits wide
endmodule

module Nor (
  input  [17:0] A,
  input  [17:0] B,
  output [17:0] Out
);

  wire [17:0] or_1_out;

  assign or_1_out = A | B;  // OR_Gate or_1, 18 bits wide
  assign Out = ~or_1_out;  // NOT_Gate not_1, 18 bits wide
endmodule

module ALU (
  input  [17:0] A,
  input  [17:0] B,
  input  [3:0] Select,
  output [17:0] Out
);

  wire [17:0] adder_1_out, and_1_out, nand_1_out, nor_1_out;

  And and_1 (.A(A), .B(B), .Out(and_1_out));
  Adder adder_1 (.B(B), .A(A), .Out(adder_1_out));
  Nor nor_1 (.A(A), .B(B), .Out(nor_1_out));
  Nand nand_1 (.A(A), .B(B), .Out(nand_1_out));
  Multiplexer #(.select(2), .width(18), .enable("false")) multiplexer_1 (
    .in0(adder_1_out), .in1(and_1_out), .in2(nand_1_out), .in3(nor_1_out), .out(Out), .sel(Select[1:0]));
endmodule

module D_Latch (
  input  D,
  input  Clk,
  output Q
);

  wire and_1_out, and_2_out, nor_1_out, not_1_out;

  not not_1 (not_1_out, D);
  and and_1 (and_1_out, D, Clk);
  and and_2 (and_2_out, Clk, not_1_out);
  nor nor_1 (nor_1_out, and_1_out, Q);
  nor nor_2 (Q, nor_1_out, and_2_out);
endmodule

module Flip_Flop (
  input  D,
  input  Clk,
  output Q
);

  wire d_latch_1_q, not_1_out;

  D_Latch d_latch_1 (.D(D), .Clk(not_1_out), .Q(d_latch_1_q));
  not not_1 (not_1_out, Clk);
  D_Latch d_latch_2 (.D(d_latch_1_q), .Clk(Clk), .Q(Q));
endmodule

module Flag_File (
  input  [1:0] CZ_In,
  input  Write_Enable,
  input  Reset,
  input  Clk,
  output [1:0] CZ_Out
);

  Load_Flag_Register Carry_Flag (.Write_Enable(Write_Enable), .Reset(Reset), .Clk(Clk), .D(CZ_In[1]), .Q(CZ_Out[1]));
  Load_Flag_Register Zero_Flag (.Write_Enable(Write_Enable), .Reset(Reset), .Clk(Clk), .D(CZ_In[0]), .Q(CZ_Out[0]));
endmodule

module Load_Flag_Register (
  input  D,
  input  Write_Enable,
  input  Reset,
  input  Clk,
  output Q
);

  wire multiplexer_1_out;

  Multiplexer #(.select(2), .enable("false")) multiplexer_1 (
    .in0(Q), .in1(D), .in2(1'b0), .in3(1'b0), .out(multiplexer_1_out), .sel({Reset, Write_Enable}));
  Flip_Flop Carry_Flag (.D(multiplexer_1_out), .Clk(Clk), .Q(Q));
endmodule
