// Logisim project and nand nor.circ as structural Verilog: 1 circuit, main circuit main
module main (
  input  [17:0] in_1,
  input  [17:0] in_2,
  input  [17:0] in_3,
  input  [17:0] in_4,
  input  [17:0] in_5,
  input  [17:0] in_6,
  output [17:0] out_7,
  output [17:0] out_8,
  output [17:0] out_9
);

  wire [17:0] and_2_out, or_1_out;

  assign out_7 = in_1 & in_2;  // AND_Gate and_1, 18 bits wide
  assign and_2_out = in_3 & in_4;  // AND_Gate and_2, 18 bits wide
  assign out_8 = ~and_2_out;  // NOT_Gate not_1, 18 bits wide
  assign or_1_out = in_5 | in_6;  // OR_Gate or_1, 18 bits wide
  assign out_9 = ~or_1_out;  // NOT_Gate not_2, 18 bits wide
endmodule
